// Logisim project Q3.circ as structural Verilog: 1 circuit, main circuit DIV_64BIT
module DIV_64BIT (
  input  start,
  input  clk,
  input  [31:0] dividend,
  input  [31:0] divisor,
  output [31:0] quotient,
  output [31:0] remainder,
  output done
);

  wire A_GE_B, CNT_ZERO, comparator_2_eq, comparator_2_gt, DONE_OUT, not_1_out;
  wire [5:0] CNT_INNER, CNT_MINUS_1, CNT_OUT, multiplexer_8_out;
  wire [31:0] A_INNER, B_OUT, multiplexer_5_out, multiplexer_6_out, multiplexer_7_out, NEXT_A_ITER, Q_INNER,
       SUB_RESULT;

  Multiplexer #(.width(32)) multiplexer_1 (
    .in0({remainder[30:0], quotient[31]}), .in1(SUB_RESULT), .out(NEXT_A_ITER), .sel(A_GE_B));
  Multiplexer #(.width(32)) multiplexer_2 (.in0(NEXT_A_ITER), .in1(remainder), .out(A_INNER), .sel(CNT_ZERO));
  Multiplexer #(.width(6)) multiplexer_3 (.in0(CNT_MINUS_1), .in1(CNT_OUT), .out(CNT_INNER), .sel(CNT_ZERO));
  Multiplexer #(.width(32)) multiplexer_4 (
    .in0({quotient[30:0], A_GE_B}), .in1(quotient), .out(Q_INNER), .sel(CNT_ZERO));
  Multiplexer #(.width(32)) multiplexer_5 (.in0(A_INNER), .in1({32{1'b0}}), .out(multiplexer_5_out), .sel(start));
  Multiplexer #(.width(32)) multiplexer_6 (.in0(Q_INNER), .in1(dividend), .out(multiplexer_6_out), .sel(start));
  Multiplexer #(.width(32)) multiplexer_7 (.in0(B_OUT), .in1(divisor), .out(multiplexer_7_out), .sel(start));
  Multiplexer #(.width(6)) multiplexer_8 (.in0(CNT_INNER), .in1(6'b100000), .out(multiplexer_8_out), .sel(start));
  Register #(.width(32)) A (.D(multiplexer_5_out), .clk(clk), .Q(remainder));  // open: en, clr
  Register #(.width(32)) Q (.D(multiplexer_6_out), .clk(clk), .Q(quotient));  // open: en, clr
  Register #(.width(32)) B (.D(multiplexer_7_out), .clk(clk), .Q(B_OUT));  // open: en, clr
  Register #(.width(6)) Counter (.D(multiplexer_8_out), .clk(clk), .Q(CNT_OUT));  // open: en, clr
  not not_1 (not_1_out, start);
  Subtractor #(.width(6)) subtractor_1 (.a(CNT_OUT), .b(6'b000001), .out(CNT_MINUS_1));  // open: bin, bout
  Comparator #(.mode("unsigned"), .width(6)) comparator_1 (.a(CNT_OUT), .b({6{1'b0}}), .eq(CNT_ZERO));  // open: gt, lt
  and and_1 (done, not_1_out, CNT_ZERO);
  D_Flip_Flop DONE_FF (.D(done), .clk(clk), .Q(DONE_OUT));  // open: Qn, preset, reset
  Register #(.width(32)) QUO_REG (.D(quotient), .en(done), .clk(clk));  // open: Q, clr
  Register #(.width(32)) REM_REG (.D(remainder), .en(done), .clk(clk));  // open: Q, clr
  Subtractor #(.width(32)) subtractor_2 (
    .a({remainder[30:0], quotient[31]}), .b(B_OUT), .out(SUB_RESULT));  // open: bin, bout
  Comparator #(.mode("unsigned"), .width(32)) comparator_2 (
    .a({remainder[30:0], quotient[31]}), .b(B_OUT), .gt(comparator_2_gt), .eq(comparator_2_eq));  // open: lt
  or or_1 (A_GE_B, comparator_2_gt, comparator_2_eq);

  // Other names for the same wires on the sheet: A_BIT31 = remainder[31]; A_OUT[31:0] = remainder;
  //   A_SHIFTED[31:0] = {remainder[30:0], quotient[31]}; Q_BIT31 = quotient[31]; Q_OUT[31:0] = quotient;
  //   A_LOW31[30:0] = remainder[30:0]; DIVIDENT[31:0] = dividend; NEXT_Q_ITER[31:0] = {quotient[30:0], A_GE_B};
  //   Q_LOW31[30:0] = quotient[30:0]; RESULT_WE = done
endmodule
