// Logisim project RegisterFile.circ as structural Verilog: 3 circuits, main circuit RegisterFile
module RegisterFile (
  input  [31:0] Data,
  input  clk,
  input  rst,
  input  [4:0] Write,
  input  WriteReg,
  input  [4:0] Read0,
  input  [4:0] Read1,
  output [31:0] Out0,
  output [31:0] Out8,
  output [31:0] Out16,
  output [31:0] Out24,
  output [31:0] Out1,
  output [31:0] Out9,
  output [31:0] Out17,
  output [31:0] Out25,
  output [31:0] Out2,
  output [31:0] Out10,
  output [31:0] Out18,
  output [31:0] Out26,
  output [31:0] Out3,
  output [31:0] Out11,
  output [31:0] Out19,
  output [31:0] Out27,
  output [31:0] Out4,
  output [31:0] Out12,
  output [31:0] Out20,
  output [31:0] Out28,
  output [31:0] Out5,
  output [31:0] Out13,
  output [31:0] Out21,
  output [31:0] Out29,
  output [31:0] Out6,
  output [31:0] Out14,
  output [31:0] Out22,
  output [31:0] Out30,
  output [31:0] Out7,
  output [31:0] Out15,
  output [31:0] Out23,
  output [31:0] Out31,
  output [31:0] RegOut1,
  output [31:0] RegOut2
);

  wire WRITE0, WRITE1, WRITE2, WRITE3, WRITE4, WRITE5, WRITE6, WRITE7, WRITE8, WRITE9, WRITE10, WRITE11,
       WRITE12, WRITE13, WRITE14, WRITE15, WRITE16, WRITE17, WRITE18, WRITE19, WRITE20, WRITE21, WRITE22,
       WRITE23, WRITE24, WRITE25, WRITE26, WRITE27, WRITE28, WRITE29, WRITE30, WRITE31;

  REG32 reg32_1 (.Data(Data), .rst(rst), .WriteEnable(1'b0), .clk(clk), .out1(Out0));
  REG32 reg32_2 (.Data(Data), .rst(rst), .WriteEnable(WRITE1), .clk(clk), .out1(Out1));
  REG32 reg32_3 (.Data(Data), .rst(rst), .WriteEnable(WRITE2), .clk(clk), .out1(Out2));
  REG32 reg32_4 (.Data(Data), .rst(rst), .WriteEnable(WRITE3), .clk(clk), .out1(Out3));
  REG32 reg32_5 (.Data(Data), .rst(rst), .WriteEnable(WRITE4), .clk(clk), .out1(Out4));
  REG32 reg32_6 (.Data(Data), .rst(rst), .WriteEnable(WRITE5), .clk(clk), .out1(Out5));
  REG32 reg32_7 (.Data(Data), .rst(rst), .WriteEnable(WRITE6), .clk(clk), .out1(Out6));
  REG32 reg32_8 (.Data(Data), .rst(rst), .WriteEnable(WRITE7), .clk(clk), .out1(Out7));
  WriteEnableDecoder writeenabledecoder_1 (
    .Write(Write), .WriteReg(WriteReg), .reg0(WRITE0), .out_4(WRITE1), .out_5(WRITE2), .out_6(WRITE3),
    .out_7(WRITE4), .out_8(WRITE5), .out_9(WRITE6), .out_10(WRITE7), .out_11(WRITE8), .out_12(WRITE9),
    .out_13(WRITE10), .out_14(WRITE11), .out_15(WRITE12), .out_16(WRITE13), .out_17(WRITE14),
    .out_18(WRITE15), .out_19(WRITE16), .out_20(WRITE17), .out_21(WRITE18), .out_22(WRITE19),
    .out_23(WRITE20), .out_24(WRITE21), .out_25(WRITE22), .out_26(WRITE23), .out_27(WRITE24),
    .out_28(WRITE25), .out_29(WRITE26), .out_30(WRITE27), .out_31(WRITE28), .out_32(WRITE29),
    .out_33(WRITE30), .out_34(WRITE31));
  REG32 reg32_9 (.Data(Data), .rst(rst), .WriteEnable(WRITE8), .clk(clk), .out1(Out8));
  REG32 reg32_10 (.Data(Data), .rst(rst), .WriteEnable(WRITE9), .clk(clk), .out1(Out9));
  REG32 reg32_11 (.Data(Data), .rst(rst), .WriteEnable(WRITE10), .clk(clk), .out1(Out10));
  REG32 reg32_12 (.Data(Data), .rst(rst), .WriteEnable(WRITE11), .clk(clk), .out1(Out11));
  REG32 reg32_13 (.Data(Data), .rst(rst), .WriteEnable(WRITE12), .clk(clk), .out1(Out12));
  REG32 reg32_14 (.Data(Data), .rst(rst), .WriteEnable(WRITE13), .clk(clk), .out1(Out13));
  REG32 reg32_15 (.Data(Data), .rst(rst), .WriteEnable(WRITE14), .clk(clk), .out1(Out14));
  REG32 reg32_16 (.Data(Data), .rst(rst), .WriteEnable(WRITE15), .clk(clk), .out1(Out15));
  Multiplexer #(.select(5), .width(32)) multiplexer_1 (
    .in0({32{1'b0}}), .in1(Out1), .in2(Out2), .in3(Out3), .in4(Out4), .in5(Out5), .in6(Out6), .in7(Out7),
    .in8(Out8), .in9(Out9), .in10(Out10), .in11(Out11), .in12(Out12), .in13(Out13), .in14(Out14),
    .in15(Out15), .in16(Out16), .in17(Out17), .in18(Out18), .in19(Out19), .in20(Out20), .in21(Out21),
    .in22(Out22), .in23(Out23), .in24(Out24), .in25(Out25), .in26(Out26), .in27(Out27), .in28(Out28),
    .in29(Out29), .in30(Out30), .in31(Out31), .out(RegOut1), .sel(Read0));
  REG32 reg32_17 (.Data(Data), .rst(rst), .WriteEnable(WRITE16), .clk(clk), .out1(Out16));
  REG32 reg32_18 (.Data(Data), .rst(rst), .WriteEnable(WRITE17), .clk(clk), .out1(Out17));
  REG32 reg32_19 (.Data(Data), .rst(rst), .WriteEnable(WRITE18), .clk(clk), .out1(Out18));
  REG32 reg32_20 (.Data(Data), .rst(rst), .WriteEnable(WRITE19), .clk(clk), .out1(Out19));
  REG32 reg32_21 (.Data(Data), .rst(rst), .WriteEnable(WRITE20), .clk(clk), .out1(Out20));
  REG32 reg32_22 (.Data(Data), .rst(rst), .WriteEnable(WRITE21), .clk(clk), .out1(Out21));
  REG32 reg32_23 (.Data(Data), .rst(rst), .WriteEnable(WRITE22), .clk(clk), .out1(Out22));
  REG32 reg32_24 (.Data(Data), .rst(rst), .WriteEnable(WRITE23), .clk(clk), .out1(Out23));
  REG32 reg32_25 (.Data(Data), .rst(rst), .WriteEnable(WRITE24), .clk(clk), .out1(Out24));
  REG32 reg32_26 (.Data(Data), .rst(rst), .WriteEnable(WRITE25), .clk(clk), .out1(Out25));
  REG32 reg32_27 (.Data(Data), .rst(rst), .WriteEnable(WRITE26), .clk(clk), .out1(Out26));
  REG32 reg32_28 (.Data(Data), .rst(rst), .WriteEnable(WRITE27), .clk(clk), .out1(Out27));
  REG32 reg32_29 (.Data(Data), .rst(rst), .WriteEnable(WRITE28), .clk(clk), .out1(Out28));
  REG32 reg32_30 (.Data(Data), .rst(rst), .WriteEnable(WRITE29), .clk(clk), .out1(Out29));
  REG32 reg32_31 (.Data(Data), .rst(rst), .WriteEnable(WRITE30), .clk(clk), .out1(Out30));
  REG32 reg32_32 (.Data(Data), .rst(rst), .WriteEnable(WRITE31), .clk(clk), .out1(Out31));
  Multiplexer #(.select(5), .width(32)) multiplexer_2 (
    .in0({32{1'b0}}), .in1(Out1), .in2(Out2), .in3(Out3), .in4(Out4), .in5(Out5), .in6(Out6), .in7(Out7),
    .in8(Out8), .in9(Out9), .in10(Out10), .in11(Out11), .in12(Out12), .in13(Out13), .in14(Out14),
    .in15(Out15), .in16(Out16), .in17(Out17), .in18(Out18), .in19(Out19), .in20(Out20), .in21(Out21),
    .in22(Out22), .in23(Out23), .in24(Out24), .in25(Out25), .in26(Out26), .in27(Out27), .in28(Out28),
    .in29(Out29), .in30(Out30), .in31(Out31), .out(RegOut2), .sel(Read1));
endmodule

module REG32 (
  input  [31:0] Data,
  input  rst,
  input  WriteEnable,
  input  clk,
  output [31:0] out1
);

  Register #(.trigger("falling"), .width(32)) register_1 (.D(Data), .en(WriteEnable), .clk(clk), .Q(out1), .clr(rst));
endmodule

module WriteEnableDecoder (
  input  [4:0] Write,
  input  WriteReg,
  output reg0,
  output out_4,
  output out_5,
  output out_6,
  output out_7,
  output out_8,
  output out_9,
  output out_10,
  output out_11,
  output out_12,
  output out_13,
  output out_14,
  output out_15,
  output out_16,
  output out_17,
  output out_18,
  output out_19,
  output out_20,
  output out_21,
  output out_22,
  output out_23,
  output out_24,
  output out_25,
  output out_26,
  output out_27,
  output out_28,
  output out_29,
  output out_30,
  output out_31,
  output out_32,
  output out_33,
  output out_34
);

  Decoder #(.select(5)) decoder_1 (
    .out0(reg0), .out1(out_4), .out2(out_5), .out3(out_6), .out4(out_7), .out5(out_8), .out6(out_9),
    .out7(out_10), .out8(out_11), .out9(out_12), .out10(out_13), .out11(out_14), .out12(out_15),
    .out13(out_16), .out14(out_17), .out15(out_18), .out16(out_19), .out17(out_20), .out18(out_21),
    .out19(out_22), .out20(out_23), .out21(out_24), .out22(out_25), .out23(out_26), .out24(out_27),
    .out25(out_28), .out26(out_29), .out27(out_30), .out28(out_31), .out29(out_32), .out30(out_33),
    .out31(out_34), .sel(Write), .en(WriteReg));
endmodule
