// Logisim project pipeline_v5.circ as structural Verilog: 10 circuits, main circuit main
module main (
  input  clk,
  input  rst,
  input  [31:0] Jin,
  input  Jen,
  output [31:0] R0,
  output [31:0] R8,
  output [31:0] R16,
  output [31:0] R24,
  output [31:0] R1,
  output [31:0] R9,
  output [31:0] R17,
  output [31:0] R25,
  output [31:0] R2,
  output [31:0] R10,
  output [31:0] R18,
  output [31:0] R26,
  output [31:0] R3,
  output [31:0] R11,
  output [31:0] R19,
  output [31:0] R27,
  output [31:0] R4,
  output [31:0] R12,
  output [31:0] R20,
  output [31:0] R28,
  output [31:0] R5,
  output [31:0] R13,
  output [31:0] R21,
  output [31:0] R29,
  output [31:0] R6,
  output [31:0] R14,
  output [3:0] test,
  output [31:0] R22,
  output [31:0] R30,
  output [31:0] R7,
  output [31:0] R15,
  output [31:0] R23,
  output [31:0] Jout,
  output [31:0] R31,
  output InstDone
);

  wire ALU_DONE, ALUSrc, BRANCH, comparator_2_eq, comparator_3_eq, EX_ALUSrc, EX_DONE, EX_IS_DIV, EX_LINK,
       EX_MemtoReg, EX_MemWrite, EX_MFHI, EX_MFLO, EX_RegDst, EX_RegWrite, EX_SHIFT, EX_SLTI, ID_DONE,
       ID_MemWrite, ID_RegWrite, IS_BNE, IS_DIV, LINK, MEM_DONE, MEM_LINK, MEM_MemtoReg, MEM_MemWrite,
       MEM_MFHI, MEM_MFLO, MEM_RegWrite, MEM_SLTI, MemtoReg, MemWrite, MFHI, MFLO, not_1_out, NOT_STALL,
       OPERANDS_EQUAL, or_1_out, RAW_SHIFT, RegDst, RegWrite, SHIFT, SHOULD_BRANCH, SLTI, STALL, WB_LINK,
       WB_MemtoReg, WB_MFHI, WB_MFLO, WB_RegWrite, WB_SLTI;
  wire [1:0] ALU_IN, branchforwardingunit_1_branchforwarda, branchforwardingunit_1_branchforwardb,
       FINAL_MemtoReg, forwardingunit_1_forwarda, forwardingunit_1_forwardb, PCSrc;
  wire [3:0] ALUOP;
  wire [4:0] DestReg, EX_REG1, EX_REG2, EX_REG3, MEM_DestReg, multiplexer_13_out, WB_DestReg;
  wire [5:0] FUNCT;
  wire [9:0] JUMP_ADDR;
  wire [31:0] ALU_HIGH, ALU_LOW, BEQ_RESULT, BranchAddr, BranchForwardMuxA, BranchForwardMuxB, EX_IMM,
       EX_PCplus1, EX_RegRead1, EX_RegRead2, EX_SHAMT, ForwardMux_A, ForwardMux_B, HI_REG, I_JOUT,
       ID_PCplus1, IMM, LOW_REG, MEM_ALU_HIGH, MEM_ALU_LOW, MEM_BRANCH_VALUE, MEM_OUT, MEM_PCplus1,
       MEM_RegRead2, multiplexer_1_out, multiplexer_3_out, multiplexer_4_out, multiplexer_7_out,
       multiplexer_8_out, PC, PCplus1, RAW_INST, RegRead1, RegRead2, SHAMT, SLTI_RESULT, WB_ALU_HIGH,
       WB_ALU_LOW, WB_MEM_OUT, WB_PCplus1, WB_WriteData;
  wire [31:6] ID_Instruction;

  Adder #(.width(32)) adder_1 (.a(32'h1), .b(PC), .out(PCplus1));  // open: cin, cout
  Adder #(.width(32)) adder_2 (.a(ID_PCplus1), .b(IMM), .out(BranchAddr));  // open: cin, cout
  Bit_Extender #(.in_width(26), .out_width(10)) bit_extender_1 (.in({ID_Instruction[25:6], FUNCT}), .out(JUMP_ADDR));
  assign SLTI_RESULT = {{31{1'b0}}, ALU_LOW[31]};  // Bit_Extender bit_extender_2
  Comparator #(.mode("unsigned"), .width(6)) comparator_1 (
    .a(ID_Instruction[31:26]), .b(6'b000101), .eq(IS_BNE));  // open: gt, lt
  Multiplexer #(.select(2), .width(32)) multiplexer_1 (
    .in0(PCplus1), .in1(BEQ_RESULT), .in2({ID_PCplus1[31:10], JUMP_ADDR}), .in3(R31),
    .out(multiplexer_1_out), .sel(PCSrc));
  not not_1 (not_1_out, comparator_2_eq);
  Comparator #(.mode("unsigned"), .width(32)) comparator_2 (
    .a(RAW_INST), .b({32{1'b0}}), .eq(comparator_2_eq));  // open: gt, lt
  and and_1 (ID_MemWrite, MemWrite, NOT_STALL);
  and and_2 (ID_RegWrite, NOT_STALL, RegWrite);
  Register #(.width(32)) u_PC (.D(multiplexer_1_out), .en(NOT_STALL), .clk(clk), .Q(PC), .clr(rst));
  ALUControlUnit alucontrolunit_1 (.alu_in(ALU_IN), .funct(FUNCT), .aluop(ALUOP), .shift(RAW_SHIFT), .is_div(IS_DIV));
  Comparator #(.mode("unsigned"), .width(6)) comparator_3 (
    .a(ID_Instruction[31:26]), .b({6{1'b0}}), .eq(comparator_3_eq));  // open: gt, lt
  Multiplexer #(.width(32)) multiplexer_2 (.in0(PCplus1), .in1(BranchAddr), .out(BEQ_RESULT), .sel(SHOULD_BRANCH));
  IF_ID if_id_1 (
    .PC(PCplus1), .Inst(RAW_INST), .done(ALU_DONE), .clk(clk), .rst(rst), .not_stall(NOT_STALL),
    .ID_PC(ID_PCplus1), .ID_Inst({ID_Instruction, FUNCT}), .ID_done(ID_DONE));
  xor xor_1 (SHOULD_BRANCH, OPERANDS_EQUAL, IS_BNE);
  and and_3 (SHIFT, not_1_out, comparator_3_eq, RAW_SHIFT);
  Comparator #(.mode("unsigned"), .width(32)) comparator_4 (
    .a(BranchForwardMuxA), .b(BranchForwardMuxB), .eq(OPERANDS_EQUAL));  // open: gt, lt
  Multiplexer #(.select(2), .width(32)) multiplexer_3 (
    .in0(ForwardMux_B), .in1(EX_IMM), .in2(EX_SHAMT), .in3(EX_SHAMT), .out(multiplexer_3_out),
    .sel({EX_SHIFT, EX_ALUSrc}));
  BranchForwardingUnit branchforwardingunit_1 (
    .ID_Rs(ID_Instruction[25:21]), .EX_Rd(DestReg), .MEM_Rd(MEM_DestReg), .WB_Rd(WB_DestReg),
    .EX_RegWrite(EX_RegWrite), .MEM_RegWrite(MEM_RegWrite), .WB_RegWrite(WB_RegWrite),
    .ID_Rt(ID_Instruction[20:16]), .BranchForwardA(branchforwardingunit_1_branchforwarda),
    .BranchForwardB(branchforwardingunit_1_branchforwardb));
  or or_1 (or_1_out, WB_MFHI, WB_MFLO);
  Multiplexer #(.width(32)) multiplexer_4 (
    .in0(ForwardMux_A), .in1(ForwardMux_B), .out(multiplexer_4_out), .sel(EX_SHIFT));
  ID_EX id_ex_1 (
    .PC(ID_PCplus1), .ReadReg1(RegRead1), .ReadReg2(RegRead2), .Reg1(ID_Instruction[25:21]),
    .Reg2(ID_Instruction[20:16]), .Reg3(ID_Instruction[15:11]), .shamt(SHAMT), .imm(IMM), .ALUSrc(ALUSrc),
    .ALUop(ALUOP), .RegDst(RegDst), .shift(SHIFT), .MemWrite(ID_MemWrite), .MemtoReg(MemtoReg),
    .RegWrite(ID_RegWrite), .link(LINK), .mfhi(MFHI), .slti(SLTI), .div(IS_DIV), .clk(clk), .rst(rst),
    .mflo(MFLO), .done(ID_DONE), .not_stall(NOT_STALL), .EX_PC(EX_PCplus1), .EX_ReadReg1(EX_RegRead1),
    .EX_ReadReg2(EX_RegRead2), .EX_Reg1(EX_REG1), .EX_Reg2(EX_REG2), .EX_Reg3(EX_REG3), .EX_shamt(EX_SHAMT),
    .EX_imm(EX_IMM), .EX_ALUSrc(EX_ALUSrc), .EX_ALUop(test), .EX_RegDst(EX_RegDst), .EX_shift(EX_SHIFT),
    .EX_MemWrite(EX_MemWrite), .EX_MemtoReg(EX_MemtoReg), .EX_RegWrite(EX_RegWrite), .EX_link(EX_LINK),
    .EX_mfhi(EX_MFHI), .EX_slti(EX_SLTI), .EX_div(EX_IS_DIV), .EX_mflo(EX_MFLO), .EX_done(EX_DONE));
  or or_2 (FINAL_MemtoReg[0], WB_MemtoReg, WB_SLTI);
  or or_3 (FINAL_MemtoReg[1], WB_SLTI, or_1_out);
  Multiplexer #(.select(2), .width(32)) multiplexer_5 (
    .in0(RegRead1), .in1(ALU_LOW), .in2(MEM_BRANCH_VALUE), .in3(WB_WriteData), .out(BranchForwardMuxA),
    .sel(branchforwardingunit_1_branchforwarda));
  assign IMM = {{16{ID_Instruction[15]}}, {ID_Instruction[15:6], FUNCT}};  // Bit_Extender bit_extender_3
  assign SHAMT = {{27{1'b0}}, ID_Instruction[10:6]};  // Bit_Extender bit_extender_4
  MipsMemory mipsmemory_1 (
    .Din(32'h1), .Jin(Jin), .Addr(PC), .clk(clk), .Wen(1'b0), .Jen(Jen), .Jout(I_JOUT), .Dout(RAW_INST));
  MipsMemory mipsmemory_2 (
    .Din(MEM_RegRead2), .Jin(I_JOUT), .Addr(MEM_ALU_LOW), .clk(clk), .Wen(MEM_MemWrite), .Jen(Jen),
    .Jout(Jout), .Dout(MEM_OUT));
  ControlUnit controlunit_1 (
    .opcode(ID_Instruction[31:26]), .funct(FUNCT), .RegDst(RegDst), .RegWrite(RegWrite), .ALUSrc(ALUSrc),
    .MemWrite(MemWrite), .MemtoReg(MemtoReg), .PCSrc(PCSrc), .alu_in(ALU_IN), .branch(BRANCH), .link(LINK),
    .mfhi(MFHI), .slti(SLTI), .mflo(MFLO));
  Multiplexer #(.select(2), .width(32)) multiplexer_6 (
    .in0(RegRead2), .in1(ALU_LOW), .in2(MEM_BRANCH_VALUE), .in3(WB_WriteData), .out(BranchForwardMuxB),
    .sel(branchforwardingunit_1_branchforwardb));
  ALU alu_1 (
    .output_inc(1'b0), .a(multiplexer_4_out), .b(multiplexer_3_out), .output_inverted(1'b0), .aluop(test),
    .clk(clk), .rst(rst), .res_low(ALU_LOW), .done(ALU_DONE), .res_high(ALU_HIGH));
  Multiplexer #(.width(32)) multiplexer_7 (.in0(WB_ALU_LOW), .in1(WB_PCplus1), .out(multiplexer_7_out), .sel(WB_LINK));
  Multiplexer #(.width(32)) multiplexer_8 (.in0(LOW_REG), .in1(HI_REG), .out(multiplexer_8_out), .sel(WB_MFHI));
  Multiplexer #(.width(5)) multiplexer_9 (.in0(EX_REG2), .in1(EX_REG3), .out(DestReg), .sel(EX_RegDst));
  EX_MEM ex_mem_1 (
    .PC(EX_PCplus1), .DestReg(DestReg), .RegRead2(EX_RegRead2), .alu_low(ALU_LOW), .alu_high(ALU_HIGH),
    .MemWrite(EX_MemWrite), .MemtoReg(EX_MemtoReg), .RegWrite(EX_RegWrite), .link(EX_LINK), .mfhi(EX_MFHI),
    .slti(EX_SLTI), .mflo(EX_MFLO), .done(EX_DONE), .clk(clk), .rst(rst), .MEM_PC(MEM_PCplus1),
    .MEM_DestReg(MEM_DestReg), .MEM_RegRead2(MEM_RegRead2), .MEM_alu_low(MEM_ALU_LOW),
    .MEM_alu_high(MEM_ALU_HIGH), .MEM_MemWrite(MEM_MemWrite), .MEM_MemtoReg(MEM_MemtoReg),
    .MEM_RegWrite(MEM_RegWrite), .MEM_link(MEM_LINK), .MEM_mfhi(MEM_MFHI), .MEM_slti(MEM_SLTI),
    .MEM_mflo(MEM_MFLO), .MEM_done(MEM_DONE));
  ForwardingUnit forwardingunit_1 (
    .EX_Rs(EX_REG1), .EX_Rt(EX_REG2), .MEM_Rd(MEM_DestReg), .MEM_RegWrite(MEM_RegWrite), .WB_Rd(WB_DestReg),
    .WB_RegWrite(WB_RegWrite), .ForwardA(forwardingunit_1_forwarda), .ForwardB(forwardingunit_1_forwardb));
  Multiplexer #(.width(32)) multiplexer_10 (
    .in0(MEM_ALU_LOW), .in1(MEM_OUT), .out(MEM_BRANCH_VALUE), .sel(MEM_MemtoReg));
  Register #(.width(32)) register_1 (.D(ALU_LOW), .en(EX_IS_DIV), .clk(clk), .Q(LOW_REG), .clr(rst));
  Register #(.width(32)) register_2 (.D(ALU_HIGH), .en(EX_IS_DIV), .clk(clk), .Q(HI_REG), .clr(rst));
  Multiplexer #(.select(2), .width(32)) multiplexer_11 (
    .in0(EX_RegRead1), .in1(WB_WriteData), .in2(MEM_ALU_LOW), .in3({32{1'b0}}), .out(ForwardMux_A),
    .sel(forwardingunit_1_forwarda));
  Multiplexer #(.select(2), .width(32)) multiplexer_12 (
    .in0(EX_RegRead2), .in1(WB_WriteData), .in2(MEM_ALU_LOW), .in3({32{1'b0}}), .out(ForwardMux_B),
    .sel(forwardingunit_1_forwardb));
  Multiplexer #(.width(5)) multiplexer_13 (.in0(WB_DestReg), .in1({5{1'b1}}), .out(multiplexer_13_out), .sel(WB_LINK));
  Multiplexer #(.select(2), .width(32)) multiplexer_14 (
    .in0(multiplexer_7_out), .in1(WB_MEM_OUT), .in2(multiplexer_8_out), .in3(SLTI_RESULT),
    .out(WB_WriteData), .sel(FINAL_MemtoReg));
  MEM_WB mem_wb_1 (
    .PC(MEM_PCplus1), .mem(MEM_OUT), .alu_low(MEM_ALU_LOW), .alu_high(MEM_ALU_HIGH),
    .MEM_DestReg(MEM_DestReg), .MemtoReg(MEM_MemtoReg), .RegWrite(MEM_RegWrite), .link(MEM_LINK),
    .mfhi(MEM_MFHI), .slti(MEM_SLTI), .mflo(MEM_MFLO), .done(MEM_DONE), .clk(clk), .rst(rst),
    .WB_PC(WB_PCplus1), .WB_mem(WB_MEM_OUT), .WB_alu_low(WB_ALU_LOW), .WB_alu_high(WB_ALU_HIGH),
    .WB_DestReg(WB_DestReg), .WB_MemtoReg(WB_MemtoReg), .WB_RegWrite(WB_RegWrite), .WB_link(WB_LINK),
    .WB_mfhi(WB_MFHI), .WB_slti(WB_SLTI), .WB_mflo(WB_MFLO), .WB_done(InstDone));
  not not_2 (NOT_STALL, STALL);
  RegisterFile registerfile_1 (
    .Data(WB_WriteData), .clk(clk), .rst(rst), .Write(multiplexer_13_out), .WriteReg(WB_RegWrite),
    .Read0(ID_Instruction[25:21]), .Read1(ID_Instruction[20:16]), .Out0(R0), .Out8(R8), .Out16(R16),
    .Out24(R24), .Out1(R1), .Out9(R9), .Out17(R17), .Out25(R25), .Out2(R2), .Out10(R10), .Out18(R18),
    .Out26(R26), .Out3(R3), .Out11(R11), .Out19(R19), .Out27(R27), .Out4(R4), .Out12(R12), .Out20(R20),
    .Out28(R28), .Out5(R5), .Out13(R13), .Out21(R21), .Out29(R29), .Out6(R6), .Out14(R14), .Out22(R22),
    .Out30(R30), .Out7(R7), .Out15(R15), .Out23(R23), .Out31(R31), .RegOut1(RegRead1), .RegOut2(RegRead2));
  Hazard_Detection hazard_detection_1 (
    .EX_MemtoReg(EX_MemtoReg), .EX_RegWrite(EX_RegWrite), .EX_REG2(EX_REG2), .ID_REG1(ID_Instruction[25:21]),
    .ID_REG2(ID_Instruction[20:16]), .Stall(STALL));

  // Other names for the same wires on the sheet: EX_ALUOP[3:0] = test; ID_Instruction[5:0] = FUNCT;
  //   RAW_IMM[15:0] = {ID_Instruction[15:6], FUNCT}; RawJump[25:0] = {ID_Instruction[25:6], FUNCT};
  //   RAW_SHAMT[4:0] = ID_Instruction[10:6]; REG3[4:0] = ID_Instruction[15:11]; REG2[4:0] = ID_Instruction[20:16];
  //   REG1[4:0] = ID_Instruction[25:21]; OPCODE[5:0] = ID_Instruction[31:26]; JUMP_ADDR[31:10] = ID_PCplus1[31:10];
  //   JUMP_REGISTER[31:0] = R31
endmodule

module ALUControlUnit (
  input  [1:0] alu_in,
  input  [5:0] funct,
  output [3:0] aluop,
  output shift,
  output is_div
);

  wire IS_ADD, IS_AND, IS_JR, IS_MFHI, IS_OR, IS_SUB, IS_XOR, not_1_out, not_2_out, not_3_out, not_4_out,
       not_5_out, not_6_out, not_7_out, not_8_out, not_9_out, not_10_out, not_11_out, not_12_out, not_13_out,
       not_14_out, not_15_out, not_16_out, not_17_out, not_18_out, not_19_out, not_20_out, not_21_out,
       not_22_out, not_23_out, not_24_out, not_25_out, not_26_out, not_27_out, not_28_out, not_29_out,
       not_30_out, not_31_out, not_32_out, not_33_out, not_34_out, not_35_out, not_36_out, not_37_out,
       not_38_out;
  wire [2:0] OPERATION;

  not not_1 (not_1_out, funct[0]);
  not not_2 (not_2_out, funct[1]);
  not not_3 (not_3_out, funct[2]);
  not not_4 (not_4_out, funct[3]);
  not not_5 (not_5_out, funct[4]);
  not not_6 (not_6_out, funct[1]);
  not not_7 (not_7_out, funct[3]);
  not not_8 (not_8_out, funct[4]);
  not not_9 (not_9_out, funct[0]);
  not not_10 (not_10_out, funct[1]);
  not not_11 (not_11_out, funct[2]);
  not not_12 (not_12_out, funct[3]);
  not not_13 (not_13_out, funct[5]);
  and and_1 (IS_ADD, not_1_out, not_2_out, not_3_out, not_4_out, not_5_out, funct[5]);
  and and_2 (IS_OR, funct[0], not_6_out, funct[2], not_7_out, not_8_out, funct[5]);
  and and_3 (IS_MFHI, not_9_out, not_10_out, not_11_out, not_12_out, funct[4], not_13_out);
  or or_1 (OPERATION[0], IS_SUB, is_div, shift, IS_OR);
  or or_2 (OPERATION[1], is_div, IS_XOR);
  or or_3 (OPERATION[2], IS_OR, IS_AND, IS_XOR);
  Multiplexer #(.select(2), .width(4)) multiplexer_1 (
    .in0(4'b0000), .in1(4'b0001), .in2({shift, OPERATION}), .in3(4'b0001), .out(aluop), .sel(alu_in));
  not not_14 (not_14_out, funct[0]);
  not not_15 (not_15_out, funct[2]);
  not not_16 (not_16_out, funct[3]);
  not not_17 (not_17_out, funct[4]);
  not not_18 (not_18_out, funct[0]);
  not not_19 (not_19_out, funct[3]);
  not not_20 (not_20_out, funct[4]);
  not not_21 (not_21_out, funct[0]);
  not not_22 (not_22_out, funct[1]);
  not not_23 (not_23_out, funct[2]);
  not not_24 (not_24_out, funct[3]);
  not not_25 (not_25_out, funct[4]);
  not not_26 (not_26_out, funct[5]);
  and and_4 (IS_SUB, not_14_out, funct[1], not_15_out, not_16_out, not_17_out, funct[5]);
  and and_5 (IS_XOR, not_18_out, funct[1], funct[2], not_19_out, not_20_out, funct[5]);
  and and_6 (shift, not_21_out, not_22_out, not_23_out, not_24_out, not_25_out, not_26_out);
  not not_27 (not_27_out, funct[0]);
  not not_28 (not_28_out, funct[1]);
  not not_29 (not_29_out, funct[3]);
  not not_30 (not_30_out, funct[4]);
  not not_31 (not_31_out, funct[0]);
  not not_32 (not_32_out, funct[2]);
  not not_33 (not_33_out, funct[5]);
  not not_34 (not_34_out, funct[0]);
  not not_35 (not_35_out, funct[1]);
  not not_36 (not_36_out, funct[2]);
  not not_37 (not_37_out, funct[4]);
  not not_38 (not_38_out, funct[5]);
  and and_7 (IS_AND, not_27_out, not_28_out, funct[2], not_29_out, not_30_out, funct[5]);
  and and_8 (is_div, not_31_out, funct[1], not_32_out, funct[3], funct[4], not_33_out);
  and and_9 (IS_JR, not_34_out, not_35_out, not_36_out, funct[3], not_37_out, not_38_out);

  // Other names for the same wires on the sheet: IS_SLL = shift; OPERATION[3] = shift
endmodule

module ControlUnit (
  input  [5:0] opcode,
  input  [5:0] funct,
  output RegDst,
  output RegWrite,
  output ALUSrc,
  output MemWrite,
  output MemtoReg,
  output [1:0] PCSrc,
  output [1:0] alu_in,
  output branch,
  output link,
  output mfhi,
  output slti,
  output mflo
);

  wire ADDI_OP, BEQ_OP, BNE_OP, comparator_11_eq, comparator_12_eq, IS_JR, IS_JUMP, J_OP, ZERO_FUNCT;

  Comparator #(.mode("unsigned"), .width(6)) comparator_1 (.a(opcode), .b({6{1'b0}}), .eq(RegDst));  // open: gt, lt
  Comparator #(.mode("unsigned"), .width(6)) comparator_2 (.a(opcode), .b(6'b001000), .eq(ADDI_OP));  // open: gt, lt
  Comparator #(.mode("unsigned"), .width(6)) comparator_3 (.a(opcode), .b(6'b001010), .eq(slti));  // open: gt, lt
  Comparator #(.mode("unsigned"), .width(6)) comparator_4 (.a(opcode), .b(6'b100011), .eq(MemtoReg));  // open: gt, lt
  Comparator #(.mode("unsigned"), .width(6)) comparator_5 (.a(opcode), .b(6'b101011), .eq(MemWrite));  // open: gt, lt
  Comparator #(.mode("unsigned"), .width(6)) comparator_6 (.a(opcode), .b(6'b000101), .eq(BNE_OP));  // open: gt, lt
  Comparator #(.mode("unsigned"), .width(6)) comparator_7 (.a(opcode), .b(6'b000010), .eq(J_OP));  // open: gt, lt
  Comparator #(.mode("unsigned"), .width(6)) comparator_8 (.a(opcode), .b(6'b000011), .eq(link));  // open: gt, lt
  Comparator #(.mode("unsigned"), .width(6)) comparator_9 (.a(funct), .b(6'b001000), .eq(ZERO_FUNCT));  // open: gt, lt
  or or_1 (IS_JUMP, J_OP, link);
  and and_1 (IS_JR, RegDst, ZERO_FUNCT);
  Comparator #(.mode("unsigned"), .width(6)) comparator_10 (.a(opcode), .b(6'b000100), .eq(BEQ_OP));  // open: gt, lt
  Comparator #(.mode("unsigned"), .width(6)) comparator_11 (
    .a(funct), .b(6'b010000), .eq(comparator_11_eq));  // open: gt, lt
  Comparator #(.mode("unsigned"), .width(6)) comparator_12 (
    .a(funct), .b(6'b010010), .eq(comparator_12_eq));  // open: gt, lt
  or or_2 (branch, BNE_OP, BEQ_OP);
  or or_3 (PCSrc[0], branch, IS_JR);
  or or_4 (PCSrc[1], IS_JR, IS_JUMP);
  or or_5 (alu_in[0], branch, slti);
  or or_6 (alu_in[1], slti, RegDst);
  and and_2 (mfhi, RegDst, comparator_11_eq);
  and and_3 (mflo, RegDst, comparator_12_eq);
  or or_7 (RegWrite, RegDst, ADDI_OP, slti, MemtoReg, link);
  or or_8 (ALUSrc, ADDI_OP, slti, MemtoReg, MemWrite);

  // Other names for the same wires on the sheet: BRANCH_OP = branch; JAL_OP = link; LW_OP = MemtoReg; RType = RegDst;
  //   SLTI_OP = slti; SW_OP = MemWrite
endmodule

module IF_ID (
  input  [31:0] PC,
  input  [31:0] Inst,
  input  done,
  input  clk,
  input  rst,
  input  not_stall,
  output [31:0] ID_PC,
  output [31:0] ID_Inst,
  output ID_done
);

  Register #(.width(32)) PCplus1 (.D(PC), .en(not_stall), .clk(clk), .Q(ID_PC), .clr(rst));
  Register #(.width(32)) Instruction (.D(Inst), .en(not_stall), .clk(clk), .Q(ID_Inst), .clr(rst));
  Register #(.width(1)) register_1 (.D(done), .en(not_stall), .clk(clk), .Q(ID_done), .clr(rst));
endmodule

module ID_EX (
  input  [31:0] PC,
  input  [31:0] ReadReg1,
  input  [31:0] ReadReg2,
  input  [4:0] Reg1,
  input  [4:0] Reg2,
  input  [4:0] Reg3,
  input  [31:0] shamt,
  input  [31:0] imm,
  input  ALUSrc,
  input  [3:0] ALUop,
  input  RegDst,
  input  shift,
  input  MemWrite,
  input  MemtoReg,
  input  RegWrite,
  input  link,
  input  mfhi,
  input  slti,
  input  div,
  input  clk,
  input  rst,
  input  mflo,
  input  done,
  input  not_stall,
  output [31:0] EX_PC,
  output [31:0] EX_ReadReg1,
  output [31:0] EX_ReadReg2,
  output [4:0] EX_Reg1,
  output [4:0] EX_Reg2,
  output [4:0] EX_Reg3,
  output [31:0] EX_shamt,
  output [31:0] EX_imm,
  output EX_ALUSrc,
  output [3:0] EX_ALUop,
  output EX_RegDst,
  output EX_shift,
  output EX_MemWrite,
  output EX_MemtoReg,
  output EX_RegWrite,
  output EX_link,
  output EX_mfhi,
  output EX_slti,
  output EX_div,
  output EX_mflo,
  output EX_done
);

  wire multiplexer_9_out, multiplexer_11_out, multiplexer_12_out, multiplexer_13_out, multiplexer_14_out,
       multiplexer_15_out, multiplexer_16_out, multiplexer_17_out, multiplexer_18_out, multiplexer_19_out,
       multiplexer_20_out, multiplexer_21_out, not_1_out;
  wire [3:0] multiplexer_10_out;
  wire [4:0] multiplexer_4_out, multiplexer_5_out, multiplexer_6_out;
  wire [31:0] multiplexer_1_out, multiplexer_2_out, multiplexer_3_out, multiplexer_7_out, multiplexer_8_out;

  not not_1 (not_1_out, not_stall);
  Multiplexer #(.width(32)) multiplexer_1 (.in0(PC), .in1({32{1'b0}}), .out(multiplexer_1_out), .sel(not_1_out));
  Multiplexer #(.width(32)) multiplexer_2 (.in0(ReadReg1), .in1({32{1'b0}}), .out(multiplexer_2_out), .sel(not_1_out));
  Multiplexer #(.width(32)) multiplexer_3 (.in0(ReadReg2), .in1({32{1'b0}}), .out(multiplexer_3_out), .sel(not_1_out));
  Multiplexer #(.width(5)) multiplexer_4 (.in0(Reg1), .in1({5{1'b0}}), .out(multiplexer_4_out), .sel(not_1_out));
  Multiplexer #(.width(5)) multiplexer_5 (.in0(Reg2), .in1({5{1'b0}}), .out(multiplexer_5_out), .sel(not_1_out));
  Multiplexer #(.width(5)) multiplexer_6 (.in0(Reg3), .in1({5{1'b0}}), .out(multiplexer_6_out), .sel(not_1_out));
  Multiplexer #(.width(32)) multiplexer_7 (.in0(shamt), .in1({32{1'b0}}), .out(multiplexer_7_out), .sel(not_1_out));
  Multiplexer #(.width(32)) multiplexer_8 (.in0(imm), .in1({32{1'b0}}), .out(multiplexer_8_out), .sel(not_1_out));
  Multiplexer multiplexer_9 (.in0(ALUSrc), .in1(1'b0), .out(multiplexer_9_out), .sel(not_1_out));
  Multiplexer #(.width(4)) multiplexer_10 (.in0(ALUop), .in1(4'b0000), .out(multiplexer_10_out), .sel(not_1_out));
  Multiplexer multiplexer_11 (.in0(RegDst), .in1(1'b0), .out(multiplexer_11_out), .sel(not_1_out));
  Multiplexer multiplexer_12 (.in0(shift), .in1(1'b0), .out(multiplexer_12_out), .sel(not_1_out));
  Multiplexer multiplexer_13 (.in0(MemWrite), .in1(1'b0), .out(multiplexer_13_out), .sel(not_1_out));
  Multiplexer multiplexer_14 (.in0(MemtoReg), .in1(1'b0), .out(multiplexer_14_out), .sel(not_1_out));
  Multiplexer multiplexer_15 (.in0(RegWrite), .in1(1'b0), .out(multiplexer_15_out), .sel(not_1_out));
  Multiplexer multiplexer_16 (.in0(link), .in1(1'b0), .out(multiplexer_16_out), .sel(not_1_out));
  Multiplexer multiplexer_17 (.in0(mfhi), .in1(1'b0), .out(multiplexer_17_out), .sel(not_1_out));
  Multiplexer multiplexer_18 (.in0(slti), .in1(1'b0), .out(multiplexer_18_out), .sel(not_1_out));
  Multiplexer multiplexer_19 (.in0(div), .in1(1'b0), .out(multiplexer_19_out), .sel(not_1_out));
  Multiplexer multiplexer_20 (.in0(mflo), .in1(1'b0), .out(multiplexer_20_out), .sel(not_1_out));
  Multiplexer multiplexer_21 (.in0(done), .in1(1'b0), .out(multiplexer_21_out), .sel(not_1_out));
  Register #(.width(32)) register_1 (.D(multiplexer_1_out), .clk(clk), .Q(EX_PC), .clr(rst));  // open: en
  Register #(.width(32)) register_2 (.D(multiplexer_2_out), .clk(clk), .Q(EX_ReadReg1), .clr(rst));  // open: en
  Register #(.width(32)) register_3 (.D(multiplexer_3_out), .clk(clk), .Q(EX_ReadReg2), .clr(rst));  // open: en
  Register #(.width(5)) register_4 (.D(multiplexer_4_out), .clk(clk), .Q(EX_Reg1), .clr(rst));  // open: en
  Register #(.width(5)) register_5 (.D(multiplexer_5_out), .clk(clk), .Q(EX_Reg2), .clr(rst));  // open: en
  Register #(.width(5)) register_6 (.D(multiplexer_6_out), .clk(clk), .Q(EX_Reg3), .clr(rst));  // open: en
  Register #(.width(32)) register_7 (.D(multiplexer_7_out), .clk(clk), .Q(EX_shamt), .clr(rst));  // open: en
  Register #(.width(32)) register_8 (.D(multiplexer_8_out), .clk(clk), .Q(EX_imm), .clr(rst));  // open: en
  Register #(.width(1)) register_9 (.D(multiplexer_9_out), .clk(clk), .Q(EX_ALUSrc), .clr(rst));  // open: en
  Register #(.width(4)) register_10 (.D(multiplexer_10_out), .clk(clk), .Q(EX_ALUop), .clr(rst));  // open: en
  Register #(.width(1)) register_11 (.D(multiplexer_11_out), .clk(clk), .Q(EX_RegDst), .clr(rst));  // open: en
  Register #(.width(1)) register_12 (.D(multiplexer_12_out), .clk(clk), .Q(EX_shift), .clr(rst));  // open: en
  Register #(.width(1)) register_13 (.D(multiplexer_13_out), .clk(clk), .Q(EX_MemWrite), .clr(rst));  // open: en
  Register #(.width(1)) register_14 (.D(multiplexer_14_out), .clk(clk), .Q(EX_MemtoReg), .clr(rst));  // open: en
  Register #(.width(1)) register_15 (.D(multiplexer_15_out), .clk(clk), .Q(EX_RegWrite), .clr(rst));  // open: en
  Register #(.width(1)) register_16 (.D(multiplexer_16_out), .clk(clk), .Q(EX_link), .clr(rst));  // open: en
  Register #(.width(1)) register_17 (.D(multiplexer_17_out), .clk(clk), .Q(EX_mfhi), .clr(rst));  // open: en
  Register #(.width(1)) register_18 (.D(multiplexer_18_out), .clk(clk), .Q(EX_slti), .clr(rst));  // open: en
  Register #(.width(1)) register_19 (.D(multiplexer_19_out), .clk(clk), .Q(EX_div), .clr(rst));  // open: en
  Register #(.width(1)) register_20 (.D(multiplexer_20_out), .clk(clk), .Q(EX_mflo), .clr(rst));  // open: en
  Register #(.width(1)) register_21 (.D(multiplexer_21_out), .clk(clk), .Q(EX_done), .clr(rst));  // open: en
endmodule

module EX_MEM (
  input  [31:0] PC,
  input  [4:0] DestReg,
  input  [31:0] RegRead2,
  input  [31:0] alu_low,
  input  [31:0] alu_high,
  input  MemWrite,
  input  MemtoReg,
  input  RegWrite,
  input  link,
  input  mfhi,
  input  slti,
  input  mflo,
  input  done,
  input  clk,
  input  rst,
  output [31:0] MEM_PC,
  output [4:0] MEM_DestReg,
  output [31:0] MEM_RegRead2,
  output [31:0] MEM_alu_low,
  output [31:0] MEM_alu_high,
  output MEM_MemWrite,
  output MEM_MemtoReg,
  output MEM_RegWrite,
  output MEM_link,
  output MEM_mfhi,
  output MEM_slti,
  output MEM_mflo,
  output MEM_done
);

  Register #(.width(32)) register_1 (.D(PC), .clk(clk), .Q(MEM_PC), .clr(rst));  // open: en
  Register #(.width(5)) register_2 (.D(DestReg), .clk(clk), .Q(MEM_DestReg), .clr(rst));  // open: en
  Register #(.width(32)) register_3 (.D(RegRead2), .clk(clk), .Q(MEM_RegRead2), .clr(rst));  // open: en
  Register #(.width(32)) register_4 (.D(alu_low), .clk(clk), .Q(MEM_alu_low), .clr(rst));  // open: en
  Register #(.width(32)) register_5 (.D(alu_high), .clk(clk), .Q(MEM_alu_high), .clr(rst));  // open: en
  Register #(.width(1)) register_6 (.D(MemWrite), .clk(clk), .Q(MEM_MemWrite), .clr(rst));  // open: en
  Register #(.width(1)) register_7 (.D(MemtoReg), .clk(clk), .Q(MEM_MemtoReg), .clr(rst));  // open: en
  Register #(.width(1)) register_8 (.D(RegWrite), .clk(clk), .Q(MEM_RegWrite), .clr(rst));  // open: en
  Register #(.width(1)) register_9 (.D(link), .clk(clk), .Q(MEM_link), .clr(rst));  // open: en
  Register #(.width(1)) register_10 (.D(mfhi), .clk(clk), .Q(MEM_mfhi), .clr(rst));  // open: en
  Register #(.width(1)) register_11 (.D(slti), .clk(clk), .Q(MEM_slti), .clr(rst));  // open: en
  Register #(.width(1)) register_12 (.D(mflo), .clk(clk), .Q(MEM_mflo), .clr(rst));  // open: en
  Register #(.width(1)) register_13 (.D(done), .clk(clk), .Q(MEM_done), .clr(rst));  // open: en
endmodule

module MEM_WB (
  input  [31:0] PC,
  input  [31:0] mem,
  input  [31:0] alu_low,
  input  [31:0] alu_high,
  input  [4:0] MEM_DestReg,
  input  MemtoReg,
  input  RegWrite,
  input  link,
  input  mfhi,
  input  slti,
  input  mflo,
  input  done,
  input  clk,
  input  rst,
  output [31:0] WB_PC,
  output [31:0] WB_mem,
  output [31:0] WB_alu_low,
  output [31:0] WB_alu_high,
  output [4:0] WB_DestReg,
  output WB_MemtoReg,
  output WB_RegWrite,
  output WB_link,
  output WB_mfhi,
  output WB_slti,
  output WB_mflo,
  output WB_done
);

  Register #(.width(32)) register_1 (.D(PC), .clk(clk), .Q(WB_PC), .clr(rst));  // open: en
  Register #(.width(32)) register_2 (.D(mem), .clk(clk), .Q(WB_mem), .clr(rst));  // open: en
  Register #(.width(32)) register_3 (.D(alu_low), .clk(clk), .Q(WB_alu_low), .clr(rst));  // open: en
  Register #(.width(32)) register_4 (.D(alu_high), .clk(clk), .Q(WB_alu_high), .clr(rst));  // open: en
  Register #(.width(5)) register_5 (.D(MEM_DestReg), .clk(clk), .Q(WB_DestReg), .clr(rst));  // open: en
  Register #(.width(1)) register_6 (.D(MemtoReg), .clk(clk), .Q(WB_MemtoReg), .clr(rst));  // open: en
  Register #(.width(1)) register_7 (.D(RegWrite), .clk(clk), .Q(WB_RegWrite), .clr(rst));  // open: en
  Register #(.width(1)) register_8 (.D(link), .clk(clk), .Q(WB_link), .clr(rst));  // open: en
  Register #(.width(1)) register_9 (.D(mfhi), .clk(clk), .Q(WB_mfhi), .clr(rst));  // open: en
  Register #(.width(1)) register_10 (.D(slti), .clk(clk), .Q(WB_slti), .clr(rst));  // open: en
  Register #(.width(1)) register_11 (.D(mflo), .clk(clk), .Q(WB_mflo), .clr(rst));  // open: en
  Register #(.width(1)) register_12 (.D(done), .clk(clk), .Q(WB_done), .clr(rst));  // open: en
endmodule

module Hazard_Detection (
  input  EX_MemtoReg,
  input  EX_RegWrite,
  input  [4:0] EX_REG2,
  input  [4:0] ID_REG1,
  input  [4:0] ID_REG2,
  output Stall
);

  wire comparator_2_eq, comparator_3_eq, Dest_Zero, Is_Load, Match, not_1_out;

  and and_1 (Is_Load, EX_MemtoReg, EX_RegWrite);
  not not_1 (not_1_out, Dest_Zero);
  Comparator #(.mode("unsigned"), .width(5)) comparator_1 (.a(EX_REG2), .b({5{1'b0}}), .eq(Dest_Zero));  // open: gt, lt
  Comparator #(.mode("unsigned"), .width(5)) comparator_2 (
    .a(EX_REG2), .b(ID_REG1), .eq(comparator_2_eq));  // open: gt, lt
  Comparator #(.mode("unsigned"), .width(5)) comparator_3 (
    .a(EX_REG2), .b(ID_REG2), .eq(comparator_3_eq));  // open: gt, lt
  and and_2 (Stall, not_1_out, Match, Is_Load);
  or or_1 (Match, comparator_2_eq, comparator_3_eq);
endmodule

module ForwardingUnit (
  input  [4:0] EX_Rs,
  input  [4:0] EX_Rt,
  input  [4:0] MEM_Rd,
  input  MEM_RegWrite,
  input  [4:0] WB_Rd,
  input  WB_RegWrite,
  output [1:0] ForwardA,
  output [1:0] ForwardB
);

  wire comparator_1_eq, comparator_2_eq, comparator_3_eq, comparator_4_eq, comparator_5_eq, comparator_6_eq,
       comparator_7_eq, comparator_8_eq, not_1_out, not_2_out, not_3_out, not_4_out, not_5_out, not_6_out;

  Comparator #(.mode("unsigned"), .width(5)) comparator_1 (
    .a(MEM_Rd), .b({5{1'b0}}), .eq(comparator_1_eq));  // open: gt, lt
  Comparator #(.mode("unsigned"), .width(5)) comparator_2 (
    .a(WB_Rd), .b({5{1'b0}}), .eq(comparator_2_eq));  // open: gt, lt
  Comparator #(.mode("unsigned"), .width(5)) comparator_3 (
    .a(MEM_Rd), .b(EX_Rs), .eq(comparator_3_eq));  // open: gt, lt
  Comparator #(.mode("unsigned"), .width(5)) comparator_4 (.a(WB_Rd), .b(EX_Rs), .eq(comparator_4_eq));  // open: gt, lt
  Comparator #(.mode("unsigned"), .width(5)) comparator_5 (
    .a(MEM_Rd), .b({5{1'b0}}), .eq(comparator_5_eq));  // open: gt, lt
  Comparator #(.mode("unsigned"), .width(5)) comparator_6 (
    .a(WB_Rd), .b({5{1'b0}}), .eq(comparator_6_eq));  // open: gt, lt
  Comparator #(.mode("unsigned"), .width(5)) comparator_7 (
    .a(MEM_Rd), .b(EX_Rt), .eq(comparator_7_eq));  // open: gt, lt
  Comparator #(.mode("unsigned"), .width(5)) comparator_8 (.a(WB_Rd), .b(EX_Rt), .eq(comparator_8_eq));  // open: gt, lt
  not not_1 (not_1_out, comparator_1_eq);
  not not_2 (not_2_out, comparator_2_eq);
  not not_3 (not_3_out, comparator_5_eq);
  not not_4 (not_4_out, comparator_6_eq);
  not not_5 (not_5_out, ForwardA[1]);
  not not_6 (not_6_out, ForwardB[1]);
  and and_1 (ForwardA[1], not_1_out, comparator_3_eq, MEM_RegWrite);
  and and_2 (ForwardA[0], not_2_out, comparator_4_eq, WB_RegWrite, not_5_out);
  and and_3 (ForwardB[1], not_3_out, comparator_7_eq, MEM_RegWrite);
  and and_4 (ForwardB[0], not_4_out, comparator_8_eq, WB_RegWrite, not_6_out);

  // Other names for the same wires on the sheet: MEM_hazard_A = ForwardA[0]; EX_hazard_A = ForwardA[1];
  //   MEM_hazard_B = ForwardB[0]; EX_hazard_B = ForwardB[1]

  // Notes on the sheet:
  //   EX_Rs: initial=0x9
  //   MEM_Rd: initial=0x9
endmodule

module BranchForwardingUnit (
  input  [4:0] ID_Rs,
  input  [4:0] EX_Rd,
  input  [4:0] MEM_Rd,
  input  [4:0] WB_Rd,
  input  EX_RegWrite,
  input  MEM_RegWrite,
  input  WB_RegWrite,
  input  [4:0] ID_Rt,
  output [1:0] BranchForwardA,
  output [1:0] BranchForwardB
);

  wire comparator_1_eq, comparator_2_eq, comparator_3_eq, comparator_4_eq, comparator_5_eq, comparator_6_eq,
       comparator_7_eq, comparator_8_eq, comparator_9_eq, EX_hazard, EX_hazard_Rt, EX_Rd_NotZero, MEM_hazard,
       MEM_hazard_Rt, MEM_Rd_NotZero, not_4_out, not_5_out, not_6_out, not_7_out, not_8_out, not_9_out,
       WB_hazard, WB_hazard_Rt, WB_Rd_NptZero;
  wire [1:0] multiplexer_1_out, multiplexer_2_out, multiplexer_3_out, multiplexer_5_out;

  Comparator #(.mode("unsigned"), .width(5)) comparator_1 (.a(ID_Rt), .b(EX_Rd), .eq(comparator_1_eq));  // open: gt, lt
  Comparator #(.mode("unsigned"), .width(5)) comparator_2 (
    .a(ID_Rt), .b(MEM_Rd), .eq(comparator_2_eq));  // open: gt, lt
  Comparator #(.mode("unsigned"), .width(5)) comparator_3 (.a(ID_Rt), .b(WB_Rd), .eq(comparator_3_eq));  // open: gt, lt
  Comparator #(.mode("unsigned"), .width(5)) comparator_4 (
    .a(EX_Rd), .b({5{1'b0}}), .eq(comparator_4_eq));  // open: gt, lt
  Comparator #(.mode("unsigned"), .width(5)) comparator_5 (.a(ID_Rs), .b(EX_Rd), .eq(comparator_5_eq));  // open: gt, lt
  Comparator #(.mode("unsigned"), .width(5)) comparator_6 (
    .a(MEM_Rd), .b({5{1'b0}}), .eq(comparator_6_eq));  // open: gt, lt
  Comparator #(.mode("unsigned"), .width(5)) comparator_7 (
    .a(ID_Rs), .b(MEM_Rd), .eq(comparator_7_eq));  // open: gt, lt
  Comparator #(.mode("unsigned"), .width(5)) comparator_8 (
    .a(WB_Rd), .b({5{1'b0}}), .eq(comparator_8_eq));  // open: gt, lt
  Comparator #(.mode("unsigned"), .width(5)) comparator_9 (.a(ID_Rs), .b(WB_Rd), .eq(comparator_9_eq));  // open: gt, lt
  not not_1 (EX_Rd_NotZero, comparator_4_eq);
  not not_2 (MEM_Rd_NotZero, comparator_6_eq);
  not not_3 (WB_Rd_NptZero, comparator_8_eq);
  not not_4 (not_4_out, EX_hazard_Rt);
  not not_5 (not_5_out, MEM_hazard_Rt);
  not not_6 (not_6_out, MEM_hazard);
  not not_7 (not_7_out, EX_hazard_Rt);
  and and_1 (EX_hazard, EX_Rd_NotZero, comparator_5_eq, EX_RegWrite);
  and and_2 (MEM_hazard, MEM_Rd_NotZero, comparator_7_eq, MEM_RegWrite, not_8_out);
  not not_8 (not_8_out, EX_hazard);
  not not_9 (not_9_out, EX_hazard);
  and and_3 (WB_hazard, WB_Rd_NptZero, comparator_9_eq, WB_RegWrite, not_6_out, not_9_out);
  and and_4 (EX_hazard_Rt, EX_Rd_NotZero, comparator_1_eq, EX_RegWrite);
  and and_5 (MEM_hazard_Rt, MEM_Rd_NotZero, comparator_2_eq, MEM_RegWrite, not_7_out);
  and and_6 (WB_hazard_Rt, comparator_3_eq, WB_Rd_NptZero, WB_RegWrite, not_4_out, not_5_out);
  Multiplexer #(.width(2)) multiplexer_1 (.in0(2'b00), .in1(2'b11), .out(multiplexer_1_out), .sel(WB_hazard));
  Multiplexer #(.width(2)) multiplexer_2 (
    .in0(multiplexer_1_out), .in1(2'b10), .out(multiplexer_2_out), .sel(MEM_hazard));
  Multiplexer #(.width(2)) multiplexer_3 (.in0(2'b00), .in1(2'b11), .out(multiplexer_3_out), .sel(WB_hazard_Rt));
  Multiplexer #(.width(2)) multiplexer_4 (.in0(multiplexer_2_out), .in1(2'b01), .out(BranchForwardA), .sel(EX_hazard));
  Multiplexer #(.width(2)) multiplexer_5 (
    .in0(multiplexer_3_out), .in1(2'b10), .out(multiplexer_5_out), .sel(MEM_hazard_Rt));
  Multiplexer #(.width(2)) multiplexer_6 (
    .in0(multiplexer_5_out), .in1(2'b01), .out(BranchForwardB), .sel(EX_hazard_Rt));
endmodule
