// Logisim project Q2.circ as structural Verilog: 7 circuits, main circuit MUL_64BIT
module CSA (
  input  [63:0] X,
  input  [63:0] Y,
  input  [63:0] Z,
  output [63:0] S_out,
  output [63:0] C_out
);

  wire [63:0] and_1_out, and_2_out, and_3_out, or_1_out;

  assign S_out = X ^ Y ^ Z;  // XOR_Gate xor_1, 64 bits wide
  assign and_1_out = X & Y;  // AND_Gate and_1, 64 bits wide
  assign and_2_out = X & Z;  // AND_Gate and_2, 64 bits wide
  assign and_3_out = Y & Z;  // AND_Gate and_3, 64 bits wide
  assign or_1_out = and_1_out | and_2_out | and_3_out;  // OR_Gate or_1, 64 bits wide
  Shifter_1bit_left shifter_1bit_left_1 (.in1(or_1_out), .out1(C_out));
endmodule

module Shifter_1bit_left (
  input  [63:0] in1,
  output [63:0] out1
);


  assign out1 = {in1[62:0], 1'b0};
endmodule

module PP_Select (
  input  [63:0] a,
  input  [1:0] b_bits,
  output [63:0] out1
);

  wire [63:0] adder_1_out, shifter_1bit_left_32bit_1_out1;

  Shifter_1bit_left_32bit shifter_1bit_left_32bit_1 (.in1(a), .out1(shifter_1bit_left_32bit_1_out1));
  Adder #(.width(64)) adder_1 (.a(shifter_1bit_left_32bit_1_out1), .b(a), .out(adder_1_out));  // open: cin, cout
  Multiplexer #(.select(2), .width(64)) multiplexer_1 (
    .in1(a), .in2(shifter_1bit_left_32bit_1_out1), .in3(adder_1_out), .out(out1), .sel(b_bits));  // open: in0
endmodule

module Shifter_1bit_left_32bit (
  input  [63:0] in1,
  output [63:0] out1
);


  assign out1 = {in1[62:0], 1'b0};
endmodule

module Shifter_2bit_left_32bit (
  input  [63:0] in1,
  output [63:0] out1
);


  assign out1 = {in1[61:0], 2'b00};
endmodule

module Shifter_2bit_right_32bit (
  input  [63:0] in1,
  output [63:0] out1
);


  assign out1 = {2'b00, in1[63:2]};
endmodule

module MUL_64BIT (
  input  [31:0] a,
  input  start,
  input  [31:0] b,
  input  rst_n,
  input  clk,
  output done,
  output [31:0] res_lo,
  output [31:0] res_hi
);

  wire and_1_out, comparator_1_lt, not_1_out, not_2_out, or_1_out, or_2_out, or_3_out, running_q;
  wire [4:0] adder_1_out, multiplexer_3_out, register_1_q;
  wire [5:0] bit_extender_3_out, bit_extender_4_out;
  wire [63:0] A_reg_q, adder_2_out, B_reg_q, bit_extender_1_out, bit_extender_2_out, C_reg_q, csa_1_c_out,
       csa_1_s_out, multiplexer_1_out, multiplexer_2_out, pp_select_1_out1, S_reg_q, shift_left_out1,
       shift_right_out1;

  not not_1 (not_1_out, rst_n);
  assign bit_extender_1_out = {{32{1'b0}}, a};  // Bit_Extender bit_extender_1
  assign bit_extender_2_out = {{32{1'b0}}, b};  // Bit_Extender bit_extender_2
  Multiplexer #(.width(64)) multiplexer_1 (
    .in0(shift_left_out1), .in1(bit_extender_1_out), .out(multiplexer_1_out), .sel(start));
  Multiplexer #(.width(64)) multiplexer_2 (
    .in0(shift_right_out1), .in1(bit_extender_2_out), .out(multiplexer_2_out), .sel(start));
  Register #(.width(64)) A_reg (.D(multiplexer_1_out), .en(or_3_out), .clk(clk), .Q(A_reg_q), .clr(not_1_out));
  Register #(.width(64)) B_reg (.D(multiplexer_2_out), .en(or_3_out), .clk(clk), .Q(B_reg_q), .clr(not_1_out));
  or or_1 (or_1_out, not_1_out, start);
  Shifter_2bit_left_32bit shift_left (.in1(A_reg_q), .out1(shift_left_out1));
  Shifter_2bit_right_32bit shift_right (.in1(B_reg_q), .out1(shift_right_out1));
  PP_Select pp_select_1 (.a(A_reg_q), .b_bits(B_reg_q[1:0]), .out1(pp_select_1_out1));
  or or_2 (or_2_out, start, and_1_out);
  Register #(.width(1)) running (.D(or_2_out), .en(1'b1), .clk(clk), .Q(running_q), .clr(not_1_out));
  Adder #(.width(5)) adder_1 (.a(register_1_q), .b(5'b00001), .out(adder_1_out), .cin(1'b0));  // open: cout
  CSA csa_1 (.X(S_reg_q), .Y(C_reg_q), .Z(pp_select_1_out1), .S_out(csa_1_s_out), .C_out(csa_1_c_out));
  Multiplexer #(.width(5)) multiplexer_3 (.in0(adder_1_out), .in1({5{1'b0}}), .out(multiplexer_3_out), .sel(start));
  and and_1 (and_1_out, running_q, not_2_out);
  or or_3 (or_3_out, running_q, start);
  Register #(.width(5)) register_1 (.D(multiplexer_3_out), .en(running_q), .clk(clk), .Q(register_1_q), .clr(or_1_out));
  Register #(.width(64)) S_reg (.D(csa_1_s_out), .en(or_3_out), .clk(clk), .Q(S_reg_q), .clr(or_1_out));
  Register #(.width(64)) C_reg (.D(csa_1_c_out), .en(or_3_out), .clk(clk), .Q(C_reg_q), .clr(or_1_out));
  assign bit_extender_3_out = {{1{1'b0}}, 5'b01111};  // Bit_Extender bit_extender_3
  not not_2 (not_2_out, done);
  Comparator #(.width(6)) comparator_1 (
    .a(bit_extender_3_out), .b(bit_extender_4_out), .lt(comparator_1_lt));  // open: gt, eq
  assign bit_extender_4_out = {{1{1'b0}}, register_1_q};  // Bit_Extender bit_extender_4
  and and_2 (done, comparator_1_lt, running_q);
  Adder #(.width(64)) adder_2 (.a(S_reg_q), .b(C_reg_q), .out(adder_2_out));  // open: cin, cout
  Register #(.width(64)) result (.D(adder_2_out), .en(done), .clk(clk), .Q({res_hi, res_lo}), .clr(or_1_out));
endmodule
