// Logisim project MipsMemory.circ as structural Verilog: 2 circuits, main circuit MipsMemory
module MipsMemory (
  input  [31:0] Din,
  input  [31:0] Jin,
  input  [31:0] Addr,
  input  clk,
  input  Wen,
  input  Jen,
  output [31:0] Jout,
  output [31:0] Dout
);

  wire G_SELECT0, G_SELECT1, G_SELECT2, G_SELECT3, G_SELECT4, G_SELECT5, G_SELECT6, G_SELECT7, G_SELECT8,
       G_SELECT9, G_SELECT10, G_SELECT11, G_SELECT12, G_SELECT13, G_SELECT14, G_SELECT15, G_SELECT16,
       G_SELECT17, G_SELECT18, G_SELECT19, G_SELECT20, G_SELECT21, G_SELECT22, G_SELECT23, G_SELECT24,
       G_SELECT25, G_SELECT26, G_SELECT27, G_SELECT28, G_SELECT29, G_SELECT30, G_SELECT31, WE;
  wire [31:0] LAST_OUT0, LAST_OUT1, LAST_OUT2, LAST_OUT3, LAST_OUT4, LAST_OUT5, LAST_OUT6, LAST_OUT7,
       LAST_OUT8, LAST_OUT9, LAST_OUT10, LAST_OUT11, LAST_OUT12, LAST_OUT13, LAST_OUT14, LAST_OUT15,
       LAST_OUT16, LAST_OUT17, LAST_OUT18, LAST_OUT19, LAST_OUT20, LAST_OUT21, LAST_OUT22, LAST_OUT23,
       LAST_OUT24, LAST_OUT25, LAST_OUT26, LAST_OUT27, LAST_OUT28, LAST_OUT29, LAST_OUT30, OUTPUT0, OUTPUT1,
       OUTPUT2, OUTPUT3, OUTPUT4, OUTPUT5, OUTPUT6, OUTPUT7, OUTPUT8, OUTPUT9, OUTPUT10, OUTPUT11, OUTPUT12,
       OUTPUT13, OUTPUT14, OUTPUT15, OUTPUT16, OUTPUT17, OUTPUT18, OUTPUT19, OUTPUT20, OUTPUT21, OUTPUT22,
       OUTPUT23, OUTPUT24, OUTPUT25, OUTPUT26, OUTPUT27, OUTPUT28, OUTPUT29, OUTPUT30, OUTPUT31, Wdata;

  or or_1 (WE, Wen, Jen);
  Multiplexer #(.width(32)) multiplexer_1 (.in0(Din), .in1(Jin), .out(Wdata), .sel(Jen));
  Decoder #(.select(5)) decoder_1 (
    .out0(G_SELECT0), .out1(G_SELECT1), .out2(G_SELECT2), .out3(G_SELECT3), .out4(G_SELECT4),
    .out5(G_SELECT5), .out6(G_SELECT6), .out7(G_SELECT7), .out8(G_SELECT8), .out9(G_SELECT9),
    .out10(G_SELECT10), .out11(G_SELECT11), .out12(G_SELECT12), .out13(G_SELECT13), .out14(G_SELECT14),
    .out15(G_SELECT15), .out16(G_SELECT16), .out17(G_SELECT17), .out18(G_SELECT18), .out19(G_SELECT19),
    .out20(G_SELECT20), .out21(G_SELECT21), .out22(G_SELECT22), .out23(G_SELECT23), .out24(G_SELECT24),
    .out25(G_SELECT25), .out26(G_SELECT26), .out27(G_SELECT27), .out28(G_SELECT28), .out29(G_SELECT29),
    .out30(G_SELECT30), .out31(G_SELECT31), .sel(Addr[8:4]), .en(WE));
  Multiplexer #(.select(5), .width(32)) multiplexer_2 (
    .in0(OUTPUT0), .in1(OUTPUT1), .in2(OUTPUT2), .in3(OUTPUT3), .in4(OUTPUT4), .in5(OUTPUT5), .in6(OUTPUT6),
    .in7(OUTPUT7), .in8(OUTPUT8), .in9(OUTPUT9), .in10(OUTPUT10), .in11(OUTPUT11), .in12(OUTPUT12),
    .in13(OUTPUT13), .in14(OUTPUT14), .in15(OUTPUT15), .in16(OUTPUT16), .in17(OUTPUT17), .in18(OUTPUT18),
    .in19(OUTPUT19), .in20(OUTPUT20), .in21(OUTPUT21), .in22(OUTPUT22), .in23(OUTPUT23), .in24(OUTPUT24),
    .in25(OUTPUT25), .in26(OUTPUT26), .in27(OUTPUT27), .in28(OUTPUT28), .in29(OUTPUT29), .in30(OUTPUT30),
    .in31(OUTPUT31), .out(Dout), .sel(Addr[8:4]));
  REG16PACK reg16pack_1 (
    .First_In(Wdata), .Wdata(Wdata), .clk(clk), .GROUP_WE(G_SELECT0), .IN_SELECT(Addr[3:0]), .JEN(Jen),
    .REG_OUT(OUTPUT0), .Last_Out(LAST_OUT0));
  REG16PACK reg16pack_2 (
    .First_In(LAST_OUT0), .Wdata(Wdata), .clk(clk), .GROUP_WE(G_SELECT1), .IN_SELECT(Addr[3:0]), .JEN(Jen),
    .REG_OUT(OUTPUT1), .Last_Out(LAST_OUT1));
  REG16PACK reg16pack_3 (
    .First_In(LAST_OUT1), .Wdata(Wdata), .clk(clk), .GROUP_WE(G_SELECT2), .IN_SELECT(Addr[3:0]), .JEN(Jen),
    .REG_OUT(OUTPUT2), .Last_Out(LAST_OUT2));
  REG16PACK reg16pack_4 (
    .First_In(LAST_OUT2), .Wdata(Wdata), .clk(clk), .GROUP_WE(G_SELECT3), .IN_SELECT(Addr[3:0]), .JEN(Jen),
    .REG_OUT(OUTPUT3), .Last_Out(LAST_OUT3));
  REG16PACK reg16pack_5 (
    .First_In(LAST_OUT3), .Wdata(Wdata), .clk(clk), .GROUP_WE(G_SELECT4), .IN_SELECT(Addr[3:0]), .JEN(Jen),
    .REG_OUT(OUTPUT4), .Last_Out(LAST_OUT4));
  REG16PACK reg16pack_6 (
    .First_In(LAST_OUT4), .Wdata(Wdata), .clk(clk), .GROUP_WE(G_SELECT5), .IN_SELECT(Addr[3:0]), .JEN(Jen),
    .REG_OUT(OUTPUT5), .Last_Out(LAST_OUT5));
  REG16PACK reg16pack_7 (
    .First_In(LAST_OUT5), .Wdata(Wdata), .clk(clk), .GROUP_WE(G_SELECT6), .IN_SELECT(Addr[3:0]), .JEN(Jen),
    .REG_OUT(OUTPUT6), .Last_Out(LAST_OUT6));
  REG16PACK reg16pack_8 (
    .First_In(LAST_OUT6), .Wdata(Wdata), .clk(clk), .GROUP_WE(G_SELECT7), .IN_SELECT(Addr[3:0]), .JEN(Jen),
    .REG_OUT(OUTPUT7), .Last_Out(LAST_OUT7));
  REG16PACK reg16pack_9 (
    .First_In(LAST_OUT7), .Wdata(Wdata), .clk(clk), .GROUP_WE(G_SELECT8), .IN_SELECT(Addr[3:0]), .JEN(Jen),
    .REG_OUT(OUTPUT8), .Last_Out(LAST_OUT8));
  REG16PACK reg16pack_10 (
    .First_In(LAST_OUT8), .Wdata(Wdata), .clk(clk), .GROUP_WE(G_SELECT9), .IN_SELECT(Addr[3:0]), .JEN(Jen),
    .REG_OUT(OUTPUT9), .Last_Out(LAST_OUT9));
  REG16PACK reg16pack_11 (
    .First_In(LAST_OUT9), .Wdata(Wdata), .clk(clk), .GROUP_WE(G_SELECT10), .IN_SELECT(Addr[3:0]), .JEN(Jen),
    .REG_OUT(OUTPUT10), .Last_Out(LAST_OUT10));
  REG16PACK reg16pack_12 (
    .First_In(LAST_OUT10), .Wdata(Wdata), .clk(clk), .GROUP_WE(G_SELECT11), .IN_SELECT(Addr[3:0]), .JEN(Jen),
    .REG_OUT(OUTPUT11), .Last_Out(LAST_OUT11));
  REG16PACK reg16pack_13 (
    .First_In(LAST_OUT11), .Wdata(Wdata), .clk(clk), .GROUP_WE(G_SELECT12), .IN_SELECT(Addr[3:0]), .JEN(Jen),
    .REG_OUT(OUTPUT12), .Last_Out(LAST_OUT12));
  REG16PACK reg16pack_14 (
    .First_In(LAST_OUT12), .Wdata(Wdata), .clk(clk), .GROUP_WE(G_SELECT13), .IN_SELECT(Addr[3:0]), .JEN(Jen),
    .REG_OUT(OUTPUT13), .Last_Out(LAST_OUT13));
  REG16PACK reg16pack_15 (
    .First_In(LAST_OUT13), .Wdata(Wdata), .clk(clk), .GROUP_WE(G_SELECT14), .IN_SELECT(Addr[3:0]), .JEN(Jen),
    .REG_OUT(OUTPUT14), .Last_Out(LAST_OUT14));
  REG16PACK reg16pack_16 (
    .First_In(LAST_OUT14), .Wdata(Wdata), .clk(clk), .GROUP_WE(G_SELECT15), .IN_SELECT(Addr[3:0]), .JEN(Jen),
    .REG_OUT(OUTPUT15), .Last_Out(LAST_OUT15));
  REG16PACK reg16pack_17 (
    .First_In(LAST_OUT15), .Wdata(Wdata), .clk(clk), .GROUP_WE(G_SELECT16), .IN_SELECT(Addr[3:0]), .JEN(Jen),
    .REG_OUT(OUTPUT16), .Last_Out(LAST_OUT16));
  REG16PACK reg16pack_18 (
    .First_In(LAST_OUT16), .Wdata(Wdata), .clk(clk), .GROUP_WE(G_SELECT17), .IN_SELECT(Addr[3:0]), .JEN(Jen),
    .REG_OUT(OUTPUT17), .Last_Out(LAST_OUT17));
  REG16PACK reg16pack_19 (
    .First_In(LAST_OUT17), .Wdata(Wdata), .clk(clk), .GROUP_WE(G_SELECT18), .IN_SELECT(Addr[3:0]), .JEN(Jen),
    .REG_OUT(OUTPUT18), .Last_Out(LAST_OUT18));
  REG16PACK reg16pack_20 (
    .First_In(LAST_OUT18), .Wdata(Wdata), .clk(clk), .GROUP_WE(G_SELECT19), .IN_SELECT(Addr[3:0]), .JEN(Jen),
    .REG_OUT(OUTPUT19), .Last_Out(LAST_OUT19));
  REG16PACK reg16pack_21 (
    .First_In(LAST_OUT19), .Wdata(Wdata), .clk(clk), .GROUP_WE(G_SELECT20), .IN_SELECT(Addr[3:0]), .JEN(Jen),
    .REG_OUT(OUTPUT20), .Last_Out(LAST_OUT20));
  REG16PACK reg16pack_22 (
    .First_In(LAST_OUT20), .Wdata(Wdata), .clk(clk), .GROUP_WE(G_SELECT21), .IN_SELECT(Addr[3:0]), .JEN(Jen),
    .REG_OUT(OUTPUT21), .Last_Out(LAST_OUT21));
  REG16PACK reg16pack_23 (
    .First_In(LAST_OUT21), .Wdata(Wdata), .clk(clk), .GROUP_WE(G_SELECT22), .IN_SELECT(Addr[3:0]), .JEN(Jen),
    .REG_OUT(OUTPUT22), .Last_Out(LAST_OUT22));
  REG16PACK reg16pack_24 (
    .First_In(LAST_OUT22), .Wdata(Wdata), .clk(clk), .GROUP_WE(G_SELECT23), .IN_SELECT(Addr[3:0]), .JEN(Jen),
    .REG_OUT(OUTPUT23), .Last_Out(LAST_OUT23));
  REG16PACK reg16pack_25 (
    .First_In(LAST_OUT23), .Wdata(Wdata), .clk(clk), .GROUP_WE(G_SELECT24), .IN_SELECT(Addr[3:0]), .JEN(Jen),
    .REG_OUT(OUTPUT24), .Last_Out(LAST_OUT24));
  REG16PACK reg16pack_26 (
    .First_In(LAST_OUT24), .Wdata(Wdata), .clk(clk), .GROUP_WE(G_SELECT25), .IN_SELECT(Addr[3:0]), .JEN(Jen),
    .REG_OUT(OUTPUT25), .Last_Out(LAST_OUT25));
  REG16PACK reg16pack_27 (
    .First_In(LAST_OUT25), .Wdata(Wdata), .clk(clk), .GROUP_WE(G_SELECT26), .IN_SELECT(Addr[3:0]), .JEN(Jen),
    .REG_OUT(OUTPUT26), .Last_Out(LAST_OUT26));
  REG16PACK reg16pack_28 (
    .First_In(LAST_OUT26), .Wdata(Wdata), .clk(clk), .GROUP_WE(G_SELECT27), .IN_SELECT(Addr[3:0]), .JEN(Jen),
    .REG_OUT(OUTPUT27), .Last_Out(LAST_OUT27));
  REG16PACK reg16pack_29 (
    .First_In(LAST_OUT27), .Wdata(Wdata), .clk(clk), .GROUP_WE(G_SELECT28), .IN_SELECT(Addr[3:0]), .JEN(Jen),
    .REG_OUT(OUTPUT28), .Last_Out(LAST_OUT28));
  REG16PACK reg16pack_30 (
    .First_In(LAST_OUT28), .Wdata(Wdata), .clk(clk), .GROUP_WE(G_SELECT29), .IN_SELECT(Addr[3:0]), .JEN(Jen),
    .REG_OUT(OUTPUT29), .Last_Out(LAST_OUT29));
  REG16PACK reg16pack_31 (
    .First_In(LAST_OUT29), .Wdata(Wdata), .clk(clk), .GROUP_WE(G_SELECT30), .IN_SELECT(Addr[3:0]), .JEN(Jen),
    .REG_OUT(OUTPUT30), .Last_Out(LAST_OUT30));
  REG16PACK reg16pack_32 (
    .First_In(LAST_OUT30), .Wdata(Wdata), .clk(clk), .GROUP_WE(G_SELECT31), .IN_SELECT(Addr[3:0]), .JEN(Jen),
    .REG_OUT(OUTPUT31), .Last_Out(Jout));

  // Other names for the same wires on the sheet: IN_SELECT[3:0] = Addr[3:0]; OUT_SELECT[4:0] = Addr[8:4];
  //   LAST_OUT31[31:0] = Jout
endmodule

module REG16PACK (
  input  [31:0] First_In,
  input  [31:0] Wdata,
  input  clk,
  input  GROUP_WE,
  input  [3:0] IN_SELECT,
  input  JEN,
  output [31:0] REG_OUT,
  output [31:0] Last_Out
);

  wire and_1_out, and_2_out, and_3_out, and_4_out, and_5_out, and_6_out, and_7_out, and_8_out, and_9_out,
       and_10_out, and_11_out, and_12_out, and_13_out, and_14_out, and_15_out, and_16_out, decoder_1_out0,
       decoder_1_out1, decoder_1_out2, decoder_1_out3, decoder_1_out4, decoder_1_out5, decoder_1_out6,
       decoder_1_out7, decoder_1_out8, decoder_1_out9, decoder_1_out10, decoder_1_out11, decoder_1_out12,
       decoder_1_out13, decoder_1_out14, decoder_1_out15, or_1_out, or_2_out, or_3_out, or_4_out, or_5_out,
       or_6_out, or_7_out, or_8_out, or_9_out, or_10_out, or_11_out, or_12_out, or_13_out, or_14_out,
       or_15_out, or_16_out;
  wire [31:0] multiplexer_1_out, multiplexer_2_out, multiplexer_3_out, multiplexer_4_out, multiplexer_5_out,
       multiplexer_6_out, multiplexer_7_out, multiplexer_8_out, multiplexer_9_out, multiplexer_10_out,
       multiplexer_11_out, multiplexer_12_out, multiplexer_13_out, multiplexer_14_out, multiplexer_15_out,
       multiplexer_16_out, register_1_q, register_2_q, register_3_q, register_4_q, register_5_q,
       register_6_q, register_7_q, register_8_q, register_9_q, register_10_q, register_11_q, register_12_q,
       register_13_q, register_14_q, register_15_q;

  Decoder #(.select(4)) decoder_1 (
    .out0(decoder_1_out0), .out1(decoder_1_out1), .out2(decoder_1_out2), .out3(decoder_1_out3),
    .out4(decoder_1_out4), .out5(decoder_1_out5), .out6(decoder_1_out6), .out7(decoder_1_out7),
    .out8(decoder_1_out8), .out9(decoder_1_out9), .out10(decoder_1_out10), .out11(decoder_1_out11),
    .out12(decoder_1_out12), .out13(decoder_1_out13), .out14(decoder_1_out14), .out15(decoder_1_out15),
    .sel(IN_SELECT), .en(1'b1));
  and and_1 (and_1_out, GROUP_WE, decoder_1_out0);
  and and_2 (and_2_out, GROUP_WE, decoder_1_out1);
  and and_3 (and_3_out, GROUP_WE, decoder_1_out2);
  and and_4 (and_4_out, GROUP_WE, decoder_1_out3);
  and and_5 (and_5_out, GROUP_WE, decoder_1_out4);
  and and_6 (and_6_out, GROUP_WE, decoder_1_out5);
  and and_7 (and_7_out, GROUP_WE, decoder_1_out6);
  and and_8 (and_8_out, GROUP_WE, decoder_1_out7);
  and and_9 (and_9_out, GROUP_WE, decoder_1_out8);
  and and_10 (and_10_out, GROUP_WE, decoder_1_out9);
  and and_11 (and_11_out, GROUP_WE, decoder_1_out10);
  and and_12 (and_12_out, GROUP_WE, decoder_1_out11);
  and and_13 (and_13_out, GROUP_WE, decoder_1_out12);
  and and_14 (and_14_out, GROUP_WE, decoder_1_out13);
  and and_15 (and_15_out, GROUP_WE, decoder_1_out14);
  and and_16 (and_16_out, GROUP_WE, decoder_1_out15);
  or or_1 (or_1_out, and_1_out, JEN);
  or or_2 (or_2_out, and_2_out, JEN);
  or or_3 (or_3_out, and_3_out, JEN);
  or or_4 (or_4_out, and_4_out, JEN);
  or or_5 (or_5_out, and_5_out, JEN);
  or or_6 (or_6_out, and_6_out, JEN);
  or or_7 (or_7_out, and_7_out, JEN);
  or or_8 (or_8_out, and_8_out, JEN);
  or or_9 (or_9_out, and_9_out, JEN);
  or or_10 (or_10_out, and_10_out, JEN);
  or or_11 (or_11_out, and_11_out, JEN);
  or or_12 (or_12_out, and_12_out, JEN);
  or or_13 (or_13_out, and_13_out, JEN);
  or or_14 (or_14_out, and_14_out, JEN);
  or or_15 (or_15_out, and_15_out, JEN);
  or or_16 (or_16_out, and_16_out, JEN);
  Register #(.width(32)) register_1 (.D(multiplexer_1_out), .en(or_1_out), .clk(clk), .Q(register_1_q));  // open: clr
  Multiplexer #(.width(32)) multiplexer_1 (.in0(Wdata), .in1(First_In), .out(multiplexer_1_out), .sel(JEN));
  Register #(.width(32)) register_2 (.D(multiplexer_2_out), .en(or_2_out), .clk(clk), .Q(register_2_q));  // open: clr
  Multiplexer #(.width(32)) multiplexer_2 (.in0(Wdata), .in1(register_1_q), .out(multiplexer_2_out), .sel(JEN));
  Register #(.width(32)) register_3 (.D(multiplexer_3_out), .en(or_3_out), .clk(clk), .Q(register_3_q));  // open: clr
  Multiplexer #(.width(32)) multiplexer_3 (.in0(Wdata), .in1(register_2_q), .out(multiplexer_3_out), .sel(JEN));
  Register #(.width(32)) register_4 (.D(multiplexer_4_out), .en(or_4_out), .clk(clk), .Q(register_4_q));  // open: clr
  Multiplexer #(.width(32)) multiplexer_4 (.in0(Wdata), .in1(register_3_q), .out(multiplexer_4_out), .sel(JEN));
  Register #(.width(32)) register_5 (.D(multiplexer_5_out), .en(or_5_out), .clk(clk), .Q(register_5_q));  // open: clr
  Multiplexer #(.width(32)) multiplexer_5 (.in0(Wdata), .in1(register_4_q), .out(multiplexer_5_out), .sel(JEN));
  Register #(.width(32)) register_6 (.D(multiplexer_6_out), .en(or_6_out), .clk(clk), .Q(register_6_q));  // open: clr
  Multiplexer #(.width(32)) multiplexer_6 (.in0(Wdata), .in1(register_5_q), .out(multiplexer_6_out), .sel(JEN));
  Register #(.width(32)) register_7 (.D(multiplexer_7_out), .en(or_7_out), .clk(clk), .Q(register_7_q));  // open: clr
  Multiplexer #(.width(32)) multiplexer_7 (.in0(Wdata), .in1(register_6_q), .out(multiplexer_7_out), .sel(JEN));
  Register #(.width(32)) register_8 (.D(multiplexer_8_out), .en(or_8_out), .clk(clk), .Q(register_8_q));  // open: clr
  Multiplexer #(.width(32)) multiplexer_8 (.in0(Wdata), .in1(register_7_q), .out(multiplexer_8_out), .sel(JEN));
  Register #(.width(32)) register_9 (.D(multiplexer_9_out), .en(or_9_out), .clk(clk), .Q(register_9_q));  // open: clr
  Multiplexer #(.width(32)) multiplexer_9 (.in0(Wdata), .in1(register_8_q), .out(multiplexer_9_out), .sel(JEN));
  Register #(.width(32)) register_10 (
    .D(multiplexer_10_out), .en(or_10_out), .clk(clk), .Q(register_10_q));  // open: clr
  Multiplexer #(.width(32)) multiplexer_10 (.in0(Wdata), .in1(register_9_q), .out(multiplexer_10_out), .sel(JEN));
  Register #(.width(32)) register_11 (
    .D(multiplexer_11_out), .en(or_11_out), .clk(clk), .Q(register_11_q));  // open: clr
  Multiplexer #(.width(32)) multiplexer_11 (.in0(Wdata), .in1(register_10_q), .out(multiplexer_11_out), .sel(JEN));
  Register #(.width(32)) register_12 (
    .D(multiplexer_12_out), .en(or_12_out), .clk(clk), .Q(register_12_q));  // open: clr
  Multiplexer #(.width(32)) multiplexer_12 (.in0(Wdata), .in1(register_11_q), .out(multiplexer_12_out), .sel(JEN));
  Register #(.width(32)) register_13 (
    .D(multiplexer_13_out), .en(or_13_out), .clk(clk), .Q(register_13_q));  // open: clr
  Multiplexer #(.width(32)) multiplexer_13 (.in0(Wdata), .in1(register_12_q), .out(multiplexer_13_out), .sel(JEN));
  Register #(.width(32)) register_14 (
    .D(multiplexer_14_out), .en(or_14_out), .clk(clk), .Q(register_14_q));  // open: clr
  Multiplexer #(.width(32)) multiplexer_14 (.in0(Wdata), .in1(register_13_q), .out(multiplexer_14_out), .sel(JEN));
  Register #(.width(32)) register_15 (
    .D(multiplexer_15_out), .en(or_15_out), .clk(clk), .Q(register_15_q));  // open: clr
  Multiplexer #(.width(32)) multiplexer_15 (.in0(Wdata), .in1(register_14_q), .out(multiplexer_15_out), .sel(JEN));
  Register #(.width(32)) register_16 (.D(multiplexer_16_out), .en(or_16_out), .clk(clk), .Q(Last_Out));  // open: clr
  Multiplexer #(.width(32)) multiplexer_16 (.in0(Wdata), .in1(register_15_q), .out(multiplexer_16_out), .sel(JEN));
  Multiplexer #(.select(4), .width(32)) multiplexer_17 (
    .in0(register_1_q), .in1(register_2_q), .in2(register_3_q), .in3(register_4_q), .in4(register_5_q),
    .in5(register_6_q), .in6(register_7_q), .in7(register_8_q), .in8(register_9_q), .in9(register_10_q),
    .in10(register_11_q), .in11(register_12_q), .in12(register_13_q), .in13(register_14_q),
    .in14(register_15_q), .in15(Last_Out), .out(REG_OUT), .sel(IN_SELECT));

  // Other names for the same wires on the sheet: DATA[31:0] = Wdata; GROUP_SELECT = GROUP_WE
endmodule
