// Logisim project ALU.circ as structural Verilog: 13 circuits, main circuit ALU
module ALU (
  input  output_inc,
  input  [31:0] a,
  input  [31:0] b,
  input  output_inverted,
  input  [3:0] aluop,
  input  clk,
  input  rst,
  output [31:0] res_low,
  output done,
  output [31:0] res_high
);

  wire ADD_DONE, AND_DONE, comparator_1_eq, comparator_2_eq, d_ff_1_q, d_ff_2_q, DIV_DONE, MUL_DONE,
       not_2_out, not_3_out, not_5_out, or_1_out, OR_DONE, ROTR_DONE, RST_t, SLL_DONE, SRA_DONE, SRL_DONE,
       START, SUB_DONE, XOR_DONE;
  wire [31:0] register_1_q, register_2_q, xor_1_out, xor_2_out;
  wire [63:0] ADD_RES, AND_RES, CLO_RES, CLZ_RES, DIV_RES, MUL_RES, multiplexer_1_out, multiplexer_2_out,
       not_4_out, OR_RES, ROTR_RES, SLL_RES, SRA_RES, SRL_RES, SUB_RES, XOR_RES;

  not not_1 (RST_t, rst);
  Register #(.width(32)) register_1 (.D(a), .clk(clk), .Q(register_1_q));  // open: en, clr
  Register #(.width(32)) register_2 (.D(b), .clk(clk), .Q(register_2_q));  // open: en, clr
  ADD_32BIT add_32bit_1 (.a(a), .b(b), .out1(ADD_RES), .done(ADD_DONE));
  SUB_32BIT sub_32bit_1 (.a(a), .b(b), .out1(SUB_RES), .done(SUB_DONE));
  AND_32BIT and_32bit_1 (.a(a), .b(b), .out1(AND_RES), .done(AND_DONE));
  OR_32BIT or_32bit_1 (.a(a), .b(b), .out1(OR_RES), .done(OR_DONE));
  CLZ_32BIT clz_32bit_1 (.a(a), .out1(CLZ_RES));
  assign xor_1_out = register_1_q ^ a;  // XOR_Gate xor_1, 32 bits wide
  Comparator #(.mode("unsigned"), .width(32)) comparator_1 (
    .a(xor_1_out), .b({32{1'b0}}), .eq(comparator_1_eq));  // open: gt, lt
  assign xor_2_out = register_2_q ^ b;  // XOR_Gate xor_2, 32 bits wide
  Comparator #(.mode("unsigned"), .width(32)) comparator_2 (
    .a(xor_2_out), .b({32{1'b0}}), .eq(comparator_2_eq));  // open: gt, lt
  not not_2 (not_2_out, comparator_2_eq);
  not not_3 (not_3_out, comparator_1_eq);
  or or_1 (or_1_out, not_3_out, not_2_out);
  SLL_32BIT sll_32bit_1 (.a(a), .b(b), .out1(SLL_RES), .done(SLL_DONE));
  ROTR_32BIT rotr_32bit_1 (.b(b), .a(a), .out1(ROTR_RES), .done(ROTR_DONE));
  XOR_32BIT xor_32bit_1 (.a(a), .b(b), .out1(XOR_RES), .done(XOR_DONE));
  SRL_32BIT srl_32bit_1 (.a(a), .b(b), .out1(SRL_RES), .done(SRL_DONE));
  CLO_32BIT clo_32bit_1 (.a(a), .out1(CLO_RES));
  assign not_4_out = ~multiplexer_1_out;  // NOT_Gate not_4, 64 bits wide
  Multiplexer #(.select(4), .width(64)) multiplexer_1 (
    .in0(ADD_RES), .in1(SUB_RES), .in2(MUL_RES), .in3(DIV_RES), .in4(AND_RES), .in5(OR_RES), .in6(XOR_RES),
    .in7(CLO_RES), .in8(CLZ_RES), .in9(SLL_RES), .in10(SRL_RES), .in11(SRA_RES), .in12(ROTR_RES),
    .out(multiplexer_1_out), .sel(aluop));  // open: in13, in14, in15
  D_Flip_Flop d_ff_1 (.D(1'b1), .clk(clk), .Q(d_ff_1_q), .reset(or_1_out));  // open: Qn, preset
  Multiplexer #(.width(64)) multiplexer_2 (
    .in0(multiplexer_1_out), .in1(not_4_out), .out(multiplexer_2_out), .sel(output_inverted));
  D_Flip_Flop d_ff_2 (.D(d_ff_1_q), .clk(clk), .Q(d_ff_2_q), .reset(or_1_out));  // open: Qn, preset
  Adder #(.width(64)) adder_1 (
    .a(multiplexer_2_out), .b({64{1'b0}}), .out({res_high, res_low}), .cin(output_inc));  // open: cout
  not not_5 (not_5_out, d_ff_2_q);
  and and_1 (START, d_ff_1_q, not_5_out);
  SRA_32BIT sra_32bit_1 (.a(a), .b(b), .out1(SRA_RES), .done(SRA_DONE));
  MUL_64BIT mul_64bit_1 (
    .a(a), .start(START), .b(b), .rst_n(RST_t), .clk(clk), .done(MUL_DONE), .res_lo(MUL_RES[31:0]),
    .res_hi(MUL_RES[63:32]));
  DIV_64BIT div_64bit_1 (
    .start(START), .clk(clk), .dividend(a), .divisor(b), .quotient(DIV_RES[31:0]),
    .remainder(DIV_RES[63:32]), .done(DIV_DONE));
  Multiplexer #(.select(4)) multiplexer_3 (
    .in0(1'b1), .in1(1'b1), .in2(MUL_DONE), .in3(DIV_DONE), .in4(1'b1), .in5(1'b1), .in6(1'b1), .in7(1'b1),
    .in8(1'b1), .in9(1'b1), .in10(1'b1), .in11(1'b1), .in12(1'b1), .out(done), .sel(aluop));  // open: in13, in14, in15
endmodule

module AND_32BIT (
  input  [31:0] a,
  input  [31:0] b,
  output [63:0] out1,
  output done
);

  wire [63:0] bit_extender_1_out, bit_extender_2_out;

  assign bit_extender_1_out = {{32{1'b0}}, a};  // Bit_Extender bit_extender_1
  assign bit_extender_2_out = {{32{1'b0}}, b};  // Bit_Extender bit_extender_2
  assign out1 = bit_extender_1_out & bit_extender_2_out;  // AND_Gate and_1, 64 bits wide

  assign done = 1'b1;
endmodule

module OR_32BIT (
  input  [31:0] a,
  input  [31:0] b,
  output [63:0] out1,
  output done
);

  wire [63:0] bit_extender_1_out, bit_extender_2_out;

  assign bit_extender_1_out = {{32{1'b0}}, a};  // Bit_Extender bit_extender_1
  assign bit_extender_2_out = {{32{1'b0}}, b};  // Bit_Extender bit_extender_2
  assign out1 = bit_extender_1_out | bit_extender_2_out;  // OR_Gate or_1, 64 bits wide

  assign done = 1'b1;
endmodule

module XOR_32BIT (
  input  [31:0] a,
  input  [31:0] b,
  output [63:0] out1,
  output done
);

  wire [63:0] bit_extender_1_out, bit_extender_2_out;

  assign bit_extender_1_out = {{32{1'b0}}, a};  // Bit_Extender bit_extender_1
  assign bit_extender_2_out = {{32{1'b0}}, b};  // Bit_Extender bit_extender_2
  assign out1 = bit_extender_1_out ^ bit_extender_2_out;  // XOR_Gate xor_1, 64 bits wide

  assign done = 1'b1;
endmodule

module CLZ (
  input  [31:0] a,
  output [63:0] out1
);

  wire [5:0] CNT_0, CNT_1, CNT_2, CNT_3, CNT_4, CNT_5, CNT_6, CNT_7, CNT_8, CNT_9, CNT_10, CNT_11, CNT_12,
       CNT_13, CNT_14, CNT_15, CNT_16, CNT_17, CNT_18, CNT_19, CNT_20, CNT_21, CNT_22, CNT_23, CNT_24,
       CNT_25, CNT_26, CNT_27, CNT_28, CNT_29, CNT_30, INC_1, INC_2, INC_3, INC_4, INC_5, INC_6, INC_7,
       INC_8, INC_9, INC_10, INC_11, INC_12, INC_13, INC_14, INC_15, INC_16, INC_17, INC_18, INC_19, INC_20,
       INC_21, INC_22, INC_23, INC_24, INC_25, INC_26, INC_27, INC_28, INC_29, INC_30, INC_31,
       multiplexer_32_out;

  Multiplexer #(.width(6)) multiplexer_1 (.in0(6'b000001), .in1({6{1'b0}}), .out(CNT_0), .sel(a[0]));
  Adder #(.width(6)) adder_1 (.a(CNT_0), .b(6'b000001), .out(INC_1));  // open: cin, cout
  Multiplexer #(.width(6)) multiplexer_2 (.in0(INC_1), .in1({6{1'b0}}), .out(CNT_1), .sel(a[1]));
  Adder #(.width(6)) adder_2 (.a(CNT_1), .b(6'b000001), .out(INC_2));  // open: cin, cout
  Multiplexer #(.width(6)) multiplexer_3 (.in0(INC_2), .in1({6{1'b0}}), .out(CNT_2), .sel(a[2]));
  Adder #(.width(6)) adder_3 (.a(CNT_2), .b(6'b000001), .out(INC_3));  // open: cin, cout
  Multiplexer #(.width(6)) multiplexer_4 (.in0(INC_3), .in1({6{1'b0}}), .out(CNT_3), .sel(a[3]));
  Adder #(.width(6)) adder_4 (.a(CNT_3), .b(6'b000001), .out(INC_4));  // open: cin, cout
  Multiplexer #(.width(6)) multiplexer_5 (.in0(INC_4), .in1({6{1'b0}}), .out(CNT_4), .sel(a[4]));
  Adder #(.width(6)) adder_5 (.a(CNT_4), .b(6'b000001), .out(INC_5));  // open: cin, cout
  Multiplexer #(.width(6)) multiplexer_6 (.in0(INC_5), .in1({6{1'b0}}), .out(CNT_5), .sel(a[5]));
  Adder #(.width(6)) adder_6 (.a(CNT_5), .b(6'b000001), .out(INC_6));  // open: cin, cout
  Multiplexer #(.width(6)) multiplexer_7 (.in0(INC_6), .in1({6{1'b0}}), .out(CNT_6), .sel(a[6]));
  Adder #(.width(6)) adder_7 (.a(CNT_6), .b(6'b000001), .out(INC_7));  // open: cin, cout
  Multiplexer #(.width(6)) multiplexer_8 (.in0(INC_7), .in1({6{1'b0}}), .out(CNT_7), .sel(a[7]));
  Adder #(.width(6)) adder_8 (.a(CNT_7), .b(6'b000001), .out(INC_8));  // open: cin, cout
  Multiplexer #(.width(6)) multiplexer_9 (.in0(INC_8), .in1({6{1'b0}}), .out(CNT_8), .sel(a[8]));
  Adder #(.width(6)) adder_9 (.a(CNT_8), .b(6'b000001), .out(INC_9));  // open: cin, cout
  Multiplexer #(.width(6)) multiplexer_10 (.in0(INC_9), .in1({6{1'b0}}), .out(CNT_9), .sel(a[9]));
  Adder #(.width(6)) adder_10 (.a(CNT_9), .b(6'b000001), .out(INC_10));  // open: cin, cout
  Multiplexer #(.width(6)) multiplexer_11 (.in0(INC_10), .in1({6{1'b0}}), .out(CNT_10), .sel(a[10]));
  Adder #(.width(6)) adder_11 (.a(CNT_10), .b(6'b000001), .out(INC_11));  // open: cin, cout
  Multiplexer #(.width(6)) multiplexer_12 (.in0(INC_11), .in1({6{1'b0}}), .out(CNT_11), .sel(a[11]));
  Adder #(.width(6)) adder_12 (.a(CNT_11), .b(6'b000001), .out(INC_12));  // open: cin, cout
  Multiplexer #(.width(6)) multiplexer_13 (.in0(INC_12), .in1({6{1'b0}}), .out(CNT_12), .sel(a[12]));
  Adder #(.width(6)) adder_13 (.a(CNT_12), .b(6'b000001), .out(INC_13));  // open: cin, cout
  Multiplexer #(.width(6)) multiplexer_14 (.in0(INC_13), .in1({6{1'b0}}), .out(CNT_13), .sel(a[13]));
  Adder #(.width(6)) adder_14 (.a(CNT_13), .b(6'b000001), .out(INC_14));  // open: cin, cout
  Multiplexer #(.width(6)) multiplexer_15 (.in0(INC_14), .in1({6{1'b0}}), .out(CNT_14), .sel(a[14]));
  Adder #(.width(6)) adder_15 (.a(CNT_14), .b(6'b000001), .out(INC_15));  // open: cin, cout
  Multiplexer #(.width(6)) multiplexer_16 (.in0(INC_15), .in1({6{1'b0}}), .out(CNT_15), .sel(a[15]));
  Adder #(.width(6)) adder_16 (.a(CNT_15), .b(6'b000001), .out(INC_16));  // open: cin, cout
  Multiplexer #(.width(6)) multiplexer_17 (.in0(INC_16), .in1({6{1'b0}}), .out(CNT_16), .sel(a[16]));
  Adder #(.width(6)) adder_17 (.a(CNT_16), .b(6'b000001), .out(INC_17));  // open: cin, cout
  Multiplexer #(.width(6)) multiplexer_18 (.in0(INC_17), .in1({6{1'b0}}), .out(CNT_17), .sel(a[17]));
  Adder #(.width(6)) adder_18 (.a(CNT_17), .b(6'b000001), .out(INC_18));  // open: cin, cout
  Multiplexer #(.width(6)) multiplexer_19 (.in0(INC_18), .in1({6{1'b0}}), .out(CNT_18), .sel(a[18]));
  Adder #(.width(6)) adder_19 (.a(CNT_18), .b(6'b000001), .out(INC_19));  // open: cin, cout
  Multiplexer #(.width(6)) multiplexer_20 (.in0(INC_19), .in1({6{1'b0}}), .out(CNT_19), .sel(a[19]));
  Adder #(.width(6)) adder_20 (.a(CNT_19), .b(6'b000001), .out(INC_20));  // open: cin, cout
  Multiplexer #(.width(6)) multiplexer_21 (.in0(INC_20), .in1({6{1'b0}}), .out(CNT_20), .sel(a[20]));
  Adder #(.width(6)) adder_21 (.a(CNT_20), .b(6'b000001), .out(INC_21));  // open: cin, cout
  Multiplexer #(.width(6)) multiplexer_22 (.in0(INC_21), .in1({6{1'b0}}), .out(CNT_21), .sel(a[21]));
  Adder #(.width(6)) adder_22 (.a(CNT_21), .b(6'b000001), .out(INC_22));  // open: cin, cout
  Multiplexer #(.width(6)) multiplexer_23 (.in0(INC_22), .in1({6{1'b0}}), .out(CNT_22), .sel(a[22]));
  Adder #(.width(6)) adder_23 (.a(CNT_22), .b(6'b000001), .out(INC_23));  // open: cin, cout
  Multiplexer #(.width(6)) multiplexer_24 (.in0(INC_23), .in1({6{1'b0}}), .out(CNT_23), .sel(a[23]));
  Adder #(.width(6)) adder_24 (.a(CNT_23), .b(6'b000001), .out(INC_24));  // open: cin, cout
  Multiplexer #(.width(6)) multiplexer_25 (.in0(INC_24), .in1({6{1'b0}}), .out(CNT_24), .sel(a[24]));
  Adder #(.width(6)) adder_25 (.a(CNT_24), .b(6'b000001), .out(INC_25));  // open: cin, cout
  Multiplexer #(.width(6)) multiplexer_26 (.in0(INC_25), .in1({6{1'b0}}), .out(CNT_25), .sel(a[25]));
  Adder #(.width(6)) adder_26 (.a(CNT_25), .b(6'b000001), .out(INC_26));  // open: cin, cout
  Multiplexer #(.width(6)) multiplexer_27 (.in0(INC_26), .in1({6{1'b0}}), .out(CNT_26), .sel(a[26]));
  Adder #(.width(6)) adder_27 (.a(CNT_26), .b(6'b000001), .out(INC_27));  // open: cin, cout
  Multiplexer #(.width(6)) multiplexer_28 (.in0(INC_27), .in1({6{1'b0}}), .out(CNT_27), .sel(a[27]));
  Adder #(.width(6)) adder_28 (.a(CNT_27), .b(6'b000001), .out(INC_28));  // open: cin, cout
  Multiplexer #(.width(6)) multiplexer_29 (.in0(INC_28), .in1({6{1'b0}}), .out(CNT_28), .sel(a[28]));
  Adder #(.width(6)) adder_29 (.a(CNT_28), .b(6'b000001), .out(INC_29));  // open: cin, cout
  Multiplexer #(.width(6)) multiplexer_30 (.in0(INC_29), .in1({6{1'b0}}), .out(CNT_29), .sel(a[29]));
  Adder #(.width(6)) adder_30 (.a(CNT_29), .b(6'b000001), .out(INC_30));  // open: cin, cout
  Multiplexer #(.width(6)) multiplexer_31 (.in0(INC_30), .in1({6{1'b0}}), .out(CNT_30), .sel(a[30]));
  Adder #(.width(6)) adder_31 (.a(CNT_30), .b(6'b000001), .out(INC_31));  // open: cin, cout
  Multiplexer #(.width(6)) multiplexer_32 (.in0(INC_31), .in1({6{1'b0}}), .out(multiplexer_32_out), .sel(a[31]));
  assign out1 = {{58{1'b0}}, multiplexer_32_out};  // Bit_Extender bit_extender_1
endmodule

module SLL_32BIT (
  input  [31:0] a,
  input  [31:0] b,
  output [63:0] out1,
  output done
);

  wire [63:0] bit_extender_1_out, multiplexer_1_out, multiplexer_2_out, multiplexer_3_out, multiplexer_4_out;

  assign bit_extender_1_out = {{32{1'b0}}, a};  // Bit_Extender bit_extender_1
  Multiplexer #(.width(64)) multiplexer_1 (
    .in0(bit_extender_1_out), .in1({bit_extender_1_out[47:0], {16{1'b0}}}), .out(multiplexer_1_out),
    .sel(b[4]));
  Multiplexer #(.width(64)) multiplexer_2 (
    .in0(multiplexer_1_out), .in1({multiplexer_1_out[55:0], {8{1'b0}}}), .out(multiplexer_2_out), .sel(b[3]));
  Multiplexer #(.width(64)) multiplexer_3 (
    .in0(multiplexer_2_out), .in1({multiplexer_2_out[59:0], 4'b0000}), .out(multiplexer_3_out), .sel(b[2]));
  Multiplexer #(.width(64)) multiplexer_4 (
    .in0(multiplexer_3_out), .in1({multiplexer_3_out[61:0], 2'b00}), .out(multiplexer_4_out), .sel(b[1]));
  Multiplexer #(.width(64)) multiplexer_5 (
    .in0(multiplexer_4_out), .in1({multiplexer_4_out[62:0], 1'b0}), .out(out1), .sel(b[0]));

  assign done = 1'b1;

  // Other names for the same wires on the sheet: B_0BIT = b[0]; B_1BIT = b[1]; B_2BIT = b[2]; B_3BIT = b[3];
  //   B_4BIT = b[4]
endmodule

module SRL_32BIT (
  input  [31:0] a,
  input  [31:0] b,
  output [63:0] out1,
  output done
);

  wire [31:0] multiplexer_1_out, multiplexer_2_out, multiplexer_3_out, multiplexer_4_out, multiplexer_5_out;

  Multiplexer #(.width(32)) multiplexer_1 (.in0(a), .in1({{16{1'b0}}, a[31:16]}), .out(multiplexer_1_out), .sel(b[4]));
  Multiplexer #(.width(32)) multiplexer_2 (
    .in0(multiplexer_1_out), .in1({{8{1'b0}}, multiplexer_1_out[31:8]}), .out(multiplexer_2_out), .sel(b[3]));
  Multiplexer #(.width(32)) multiplexer_3 (
    .in0(multiplexer_2_out), .in1({4'b0000, multiplexer_2_out[31:4]}), .out(multiplexer_3_out), .sel(b[2]));
  Multiplexer #(.width(32)) multiplexer_4 (
    .in0(multiplexer_3_out), .in1({2'b00, multiplexer_3_out[31:2]}), .out(multiplexer_4_out), .sel(b[1]));
  Multiplexer #(.width(32)) multiplexer_5 (
    .in0(multiplexer_4_out), .in1({1'b0, multiplexer_4_out[31:1]}), .out(multiplexer_5_out), .sel(b[0]));
  assign out1 = {{32{1'b0}}, multiplexer_5_out};  // Bit_Extender bit_extender_1

  assign done = 1'b1;

  // Other names for the same wires on the sheet: B_0BIT = b[0]; B_1BIT = b[1]; B_2BIT = b[2]; B_3BIT = b[3];
  //   B_4BIT = b[4]
endmodule

module SRA_32BIT (
  input  [31:0] a,
  input  [31:0] b,
  output [63:0] out1,
  output done
);

  wire [31:0] multiplexer_1_out, multiplexer_2_out, multiplexer_3_out, multiplexer_4_out, multiplexer_5_out;

  Multiplexer #(.width(32)) multiplexer_1 (.in0(a), .in1({{17{a[31]}}, a[30:16]}), .out(multiplexer_1_out), .sel(b[4]));
  Multiplexer #(.width(32)) multiplexer_2 (
    .in0(multiplexer_1_out), .in1({{9{multiplexer_1_out[31]}}, multiplexer_1_out[30:8]}),
    .out(multiplexer_2_out), .sel(b[3]));
  Multiplexer #(.width(32)) multiplexer_3 (
    .in0(multiplexer_2_out), .in1({{5{multiplexer_2_out[31]}}, multiplexer_2_out[30:4]}),
    .out(multiplexer_3_out), .sel(b[2]));
  Multiplexer #(.width(32)) multiplexer_4 (
    .in0(multiplexer_3_out), .in1({{3{multiplexer_3_out[31]}}, multiplexer_3_out[30:2]}),
    .out(multiplexer_4_out), .sel(b[1]));
  Multiplexer #(.width(32)) multiplexer_5 (
    .in0(multiplexer_4_out), .in1({{2{multiplexer_4_out[31]}}, multiplexer_4_out[30:1]}),
    .out(multiplexer_5_out), .sel(b[0]));
  assign out1 = {{32{multiplexer_5_out[31]}}, multiplexer_5_out};  // Bit_Extender bit_extender_1

  assign done = 1'b1;

  // Other names for the same wires on the sheet: B_0BIT = b[0]; B_1BIT = b[1]; B_2BIT = b[2]; B_3BIT = b[3];
  //   B_4BIT = b[4]
endmodule

module ADD_32BIT (
  input  [31:0] a,
  input  [31:0] b,
  output [63:0] out1,
  output done
);

  wire [63:0] bit_extender_1_out, bit_extender_2_out;

  assign bit_extender_1_out = {{32{1'b0}}, a};  // Bit_Extender bit_extender_1
  assign bit_extender_2_out = {{32{1'b0}}, b};  // Bit_Extender bit_extender_2
  Adder #(.width(64)) adder_1 (.a(bit_extender_1_out), .b(bit_extender_2_out), .out(out1));  // open: cin, cout

  assign done = 1'b1;
endmodule

module SUB_32BIT (
  input  [31:0] a,
  input  [31:0] b,
  output [63:0] out1,
  output done
);

  wire [63:0] bit_extender_1_out, bit_extender_2_out;

  assign bit_extender_1_out = {{32{1'b0}}, a};  // Bit_Extender bit_extender_1
  assign bit_extender_2_out = {{32{1'b0}}, b};  // Bit_Extender bit_extender_2
  Subtractor #(.width(64)) subtractor_1 (
    .a(bit_extender_1_out), .b(bit_extender_2_out), .out(out1));  // open: bin, bout

  assign done = 1'b1;
endmodule

module CLZ_32BIT (
  input  [31:0] a,
  output [63:0] out1
);

  wire [5:0] CNT_0, CNT_1, CNT_2, CNT_3, CNT_4, CNT_5, CNT_6, CNT_7, CNT_8, CNT_9, CNT_10, CNT_11, CNT_12,
       CNT_13, CNT_14, CNT_15, CNT_16, CNT_17, CNT_18, CNT_19, CNT_20, CNT_21, CNT_22, CNT_23, CNT_24,
       CNT_25, CNT_26, CNT_27, CNT_28, CNT_29, CNT_30, INC_1, INC_2, INC_3, INC_4, INC_5, INC_6, INC_7,
       INC_8, INC_9, INC_10, INC_11, INC_12, INC_13, INC_14, INC_15, INC_16, INC_17, INC_18, INC_19, INC_20,
       INC_21, INC_22, INC_23, INC_24, INC_25, INC_26, INC_27, INC_28, INC_29, INC_30, INC_31,
       multiplexer_32_out;

  Multiplexer #(.width(6)) multiplexer_1 (.in0(6'b000001), .in1({6{1'b0}}), .out(CNT_0), .sel(a[0]));
  Adder #(.width(6)) adder_1 (.a(CNT_0), .b(6'b000001), .out(INC_1));  // open: cin, cout
  Multiplexer #(.width(6)) multiplexer_2 (.in0(INC_1), .in1({6{1'b0}}), .out(CNT_1), .sel(a[1]));
  Adder #(.width(6)) adder_2 (.a(CNT_1), .b(6'b000001), .out(INC_2));  // open: cin, cout
  Multiplexer #(.width(6)) multiplexer_3 (.in0(INC_2), .in1({6{1'b0}}), .out(CNT_2), .sel(a[2]));
  Adder #(.width(6)) adder_3 (.a(CNT_2), .b(6'b000001), .out(INC_3));  // open: cin, cout
  Multiplexer #(.width(6)) multiplexer_4 (.in0(INC_3), .in1({6{1'b0}}), .out(CNT_3), .sel(a[3]));
  Adder #(.width(6)) adder_4 (.a(CNT_3), .b(6'b000001), .out(INC_4));  // open: cin, cout
  Multiplexer #(.width(6)) multiplexer_5 (.in0(INC_4), .in1({6{1'b0}}), .out(CNT_4), .sel(a[4]));
  Adder #(.width(6)) adder_5 (.a(CNT_4), .b(6'b000001), .out(INC_5));  // open: cin, cout
  Multiplexer #(.width(6)) multiplexer_6 (.in0(INC_5), .in1({6{1'b0}}), .out(CNT_5), .sel(a[5]));
  Adder #(.width(6)) adder_6 (.a(CNT_5), .b(6'b000001), .out(INC_6));  // open: cin, cout
  Multiplexer #(.width(6)) multiplexer_7 (.in0(INC_6), .in1({6{1'b0}}), .out(CNT_6), .sel(a[6]));
  Adder #(.width(6)) adder_7 (.a(CNT_6), .b(6'b000001), .out(INC_7));  // open: cin, cout
  Multiplexer #(.width(6)) multiplexer_8 (.in0(INC_7), .in1({6{1'b0}}), .out(CNT_7), .sel(a[7]));
  Adder #(.width(6)) adder_8 (.a(CNT_7), .b(6'b000001), .out(INC_8));  // open: cin, cout
  Multiplexer #(.width(6)) multiplexer_9 (.in0(INC_8), .in1({6{1'b0}}), .out(CNT_8), .sel(a[8]));
  Adder #(.width(6)) adder_9 (.a(CNT_8), .b(6'b000001), .out(INC_9));  // open: cin, cout
  Multiplexer #(.width(6)) multiplexer_10 (.in0(INC_9), .in1({6{1'b0}}), .out(CNT_9), .sel(a[9]));
  Adder #(.width(6)) adder_10 (.a(CNT_9), .b(6'b000001), .out(INC_10));  // open: cin, cout
  Multiplexer #(.width(6)) multiplexer_11 (.in0(INC_10), .in1({6{1'b0}}), .out(CNT_10), .sel(a[10]));
  Adder #(.width(6)) adder_11 (.a(CNT_10), .b(6'b000001), .out(INC_11));  // open: cin, cout
  Multiplexer #(.width(6)) multiplexer_12 (.in0(INC_11), .in1({6{1'b0}}), .out(CNT_11), .sel(a[11]));
  Adder #(.width(6)) adder_12 (.a(CNT_11), .b(6'b000001), .out(INC_12));  // open: cin, cout
  Multiplexer #(.width(6)) multiplexer_13 (.in0(INC_12), .in1({6{1'b0}}), .out(CNT_12), .sel(a[12]));
  Adder #(.width(6)) adder_13 (.a(CNT_12), .b(6'b000001), .out(INC_13));  // open: cin, cout
  Multiplexer #(.width(6)) multiplexer_14 (.in0(INC_13), .in1({6{1'b0}}), .out(CNT_13), .sel(a[13]));
  Adder #(.width(6)) adder_14 (.a(CNT_13), .b(6'b000001), .out(INC_14));  // open: cin, cout
  Multiplexer #(.width(6)) multiplexer_15 (.in0(INC_14), .in1({6{1'b0}}), .out(CNT_14), .sel(a[14]));
  Adder #(.width(6)) adder_15 (.a(CNT_14), .b(6'b000001), .out(INC_15));  // open: cin, cout
  Multiplexer #(.width(6)) multiplexer_16 (.in0(INC_15), .in1({6{1'b0}}), .out(CNT_15), .sel(a[15]));
  Adder #(.width(6)) adder_16 (.a(CNT_15), .b(6'b000001), .out(INC_16));  // open: cin, cout
  Multiplexer #(.width(6)) multiplexer_17 (.in0(INC_16), .in1({6{1'b0}}), .out(CNT_16), .sel(a[16]));
  Adder #(.width(6)) adder_17 (.a(CNT_16), .b(6'b000001), .out(INC_17));  // open: cin, cout
  Multiplexer #(.width(6)) multiplexer_18 (.in0(INC_17), .in1({6{1'b0}}), .out(CNT_17), .sel(a[17]));
  Adder #(.width(6)) adder_18 (.a(CNT_17), .b(6'b000001), .out(INC_18));  // open: cin, cout
  Multiplexer #(.width(6)) multiplexer_19 (.in0(INC_18), .in1({6{1'b0}}), .out(CNT_18), .sel(a[18]));
  Adder #(.width(6)) adder_19 (.a(CNT_18), .b(6'b000001), .out(INC_19));  // open: cin, cout
  Multiplexer #(.width(6)) multiplexer_20 (.in0(INC_19), .in1({6{1'b0}}), .out(CNT_19), .sel(a[19]));
  Adder #(.width(6)) adder_20 (.a(CNT_19), .b(6'b000001), .out(INC_20));  // open: cin, cout
  Multiplexer #(.width(6)) multiplexer_21 (.in0(INC_20), .in1({6{1'b0}}), .out(CNT_20), .sel(a[20]));
  Adder #(.width(6)) adder_21 (.a(CNT_20), .b(6'b000001), .out(INC_21));  // open: cin, cout
  Multiplexer #(.width(6)) multiplexer_22 (.in0(INC_21), .in1({6{1'b0}}), .out(CNT_21), .sel(a[21]));
  Adder #(.width(6)) adder_22 (.a(CNT_21), .b(6'b000001), .out(INC_22));  // open: cin, cout
  Multiplexer #(.width(6)) multiplexer_23 (.in0(INC_22), .in1({6{1'b0}}), .out(CNT_22), .sel(a[22]));
  Adder #(.width(6)) adder_23 (.a(CNT_22), .b(6'b000001), .out(INC_23));  // open: cin, cout
  Multiplexer #(.width(6)) multiplexer_24 (.in0(INC_23), .in1({6{1'b0}}), .out(CNT_23), .sel(a[23]));
  Adder #(.width(6)) adder_24 (.a(CNT_23), .b(6'b000001), .out(INC_24));  // open: cin, cout
  Multiplexer #(.width(6)) multiplexer_25 (.in0(INC_24), .in1({6{1'b0}}), .out(CNT_24), .sel(a[24]));
  Adder #(.width(6)) adder_25 (.a(CNT_24), .b(6'b000001), .out(INC_25));  // open: cin, cout
  Multiplexer #(.width(6)) multiplexer_26 (.in0(INC_25), .in1({6{1'b0}}), .out(CNT_25), .sel(a[25]));
  Adder #(.width(6)) adder_26 (.a(CNT_25), .b(6'b000001), .out(INC_26));  // open: cin, cout
  Multiplexer #(.width(6)) multiplexer_27 (.in0(INC_26), .in1({6{1'b0}}), .out(CNT_26), .sel(a[26]));
  Adder #(.width(6)) adder_27 (.a(CNT_26), .b(6'b000001), .out(INC_27));  // open: cin, cout
  Multiplexer #(.width(6)) multiplexer_28 (.in0(INC_27), .in1({6{1'b0}}), .out(CNT_27), .sel(a[27]));
  Adder #(.width(6)) adder_28 (.a(CNT_27), .b(6'b000001), .out(INC_28));  // open: cin, cout
  Multiplexer #(.width(6)) multiplexer_29 (.in0(INC_28), .in1({6{1'b0}}), .out(CNT_28), .sel(a[28]));
  Adder #(.width(6)) adder_29 (.a(CNT_28), .b(6'b000001), .out(INC_29));  // open: cin, cout
  Multiplexer #(.width(6)) multiplexer_30 (.in0(INC_29), .in1({6{1'b0}}), .out(CNT_29), .sel(a[29]));
  Adder #(.width(6)) adder_30 (.a(CNT_29), .b(6'b000001), .out(INC_30));  // open: cin, cout
  Multiplexer #(.width(6)) multiplexer_31 (.in0(INC_30), .in1({6{1'b0}}), .out(CNT_30), .sel(a[30]));
  Adder #(.width(6)) adder_31 (.a(CNT_30), .b(6'b000001), .out(INC_31));  // open: cin, cout
  Multiplexer #(.width(6)) multiplexer_32 (.in0(INC_31), .in1({6{1'b0}}), .out(multiplexer_32_out), .sel(a[31]));
  assign out1 = {{58{1'b0}}, multiplexer_32_out};  // Bit_Extender bit_extender_1
endmodule

module CLO_32BIT (
  input  [31:0] a,
  output [63:0] out1
);

  wire [5:0] CNT_0, CNT_1, CNT_2, CNT_3, CNT_4, CNT_5, CNT_6, CNT_7, CNT_8, CNT_9, CNT_10, CNT_11, CNT_12,
       CNT_13, CNT_14, CNT_15, CNT_16, CNT_17, CNT_18, CNT_19, CNT_20, CNT_21, CNT_22, CNT_23, CNT_24,
       CNT_25, CNT_26, CNT_27, CNT_28, CNT_29, CNT_30, INC_1, INC_2, INC_3, INC_4, INC_5, INC_6, INC_7,
       INC_8, INC_9, INC_10, INC_11, INC_12, INC_13, INC_14, INC_15, INC_16, INC_17, INC_18, INC_19, INC_20,
       INC_21, INC_22, INC_23, INC_24, INC_25, INC_26, INC_27, INC_28, INC_29, INC_30, INC_31,
       multiplexer_32_out;
  wire [31:0] not_1_out;

  assign not_1_out = ~a;  // NOT_Gate not_1, 32 bits wide
  Multiplexer #(.width(6)) multiplexer_1 (.in0(6'b000001), .in1({6{1'b0}}), .out(CNT_0), .sel(not_1_out[0]));
  Adder #(.width(6)) adder_1 (.a(CNT_0), .b(6'b000001), .out(INC_1));  // open: cin, cout
  Multiplexer #(.width(6)) multiplexer_2 (.in0(INC_1), .in1({6{1'b0}}), .out(CNT_1), .sel(not_1_out[1]));
  Adder #(.width(6)) adder_2 (.a(CNT_1), .b(6'b000001), .out(INC_2));  // open: cin, cout
  Multiplexer #(.width(6)) multiplexer_3 (.in0(INC_2), .in1({6{1'b0}}), .out(CNT_2), .sel(not_1_out[2]));
  Adder #(.width(6)) adder_3 (.a(CNT_2), .b(6'b000001), .out(INC_3));  // open: cin, cout
  Multiplexer #(.width(6)) multiplexer_4 (.in0(INC_3), .in1({6{1'b0}}), .out(CNT_3), .sel(not_1_out[3]));
  Adder #(.width(6)) adder_4 (.a(CNT_3), .b(6'b000001), .out(INC_4));  // open: cin, cout
  Multiplexer #(.width(6)) multiplexer_5 (.in0(INC_4), .in1({6{1'b0}}), .out(CNT_4), .sel(not_1_out[4]));
  Adder #(.width(6)) adder_5 (.a(CNT_4), .b(6'b000001), .out(INC_5));  // open: cin, cout
  Multiplexer #(.width(6)) multiplexer_6 (.in0(INC_5), .in1({6{1'b0}}), .out(CNT_5), .sel(not_1_out[5]));
  Adder #(.width(6)) adder_6 (.a(CNT_5), .b(6'b000001), .out(INC_6));  // open: cin, cout
  Multiplexer #(.width(6)) multiplexer_7 (.in0(INC_6), .in1({6{1'b0}}), .out(CNT_6), .sel(not_1_out[6]));
  Adder #(.width(6)) adder_7 (.a(CNT_6), .b(6'b000001), .out(INC_7));  // open: cin, cout
  Multiplexer #(.width(6)) multiplexer_8 (.in0(INC_7), .in1({6{1'b0}}), .out(CNT_7), .sel(not_1_out[7]));
  Adder #(.width(6)) adder_8 (.a(CNT_7), .b(6'b000001), .out(INC_8));  // open: cin, cout
  Multiplexer #(.width(6)) multiplexer_9 (.in0(INC_8), .in1({6{1'b0}}), .out(CNT_8), .sel(not_1_out[8]));
  Adder #(.width(6)) adder_9 (.a(CNT_8), .b(6'b000001), .out(INC_9));  // open: cin, cout
  Multiplexer #(.width(6)) multiplexer_10 (.in0(INC_9), .in1({6{1'b0}}), .out(CNT_9), .sel(not_1_out[9]));
  Adder #(.width(6)) adder_10 (.a(CNT_9), .b(6'b000001), .out(INC_10));  // open: cin, cout
  Multiplexer #(.width(6)) multiplexer_11 (.in0(INC_10), .in1({6{1'b0}}), .out(CNT_10), .sel(not_1_out[10]));
  Adder #(.width(6)) adder_11 (.a(CNT_10), .b(6'b000001), .out(INC_11));  // open: cin, cout
  Multiplexer #(.width(6)) multiplexer_12 (.in0(INC_11), .in1({6{1'b0}}), .out(CNT_11), .sel(not_1_out[11]));
  Adder #(.width(6)) adder_12 (.a(CNT_11), .b(6'b000001), .out(INC_12));  // open: cin, cout
  Multiplexer #(.width(6)) multiplexer_13 (.in0(INC_12), .in1({6{1'b0}}), .out(CNT_12), .sel(not_1_out[12]));
  Adder #(.width(6)) adder_13 (.a(CNT_12), .b(6'b000001), .out(INC_13));  // open: cin, cout
  Multiplexer #(.width(6)) multiplexer_14 (.in0(INC_13), .in1({6{1'b0}}), .out(CNT_13), .sel(not_1_out[13]));
  Adder #(.width(6)) adder_14 (.a(CNT_13), .b(6'b000001), .out(INC_14));  // open: cin, cout
  Multiplexer #(.width(6)) multiplexer_15 (.in0(INC_14), .in1({6{1'b0}}), .out(CNT_14), .sel(not_1_out[14]));
  Adder #(.width(6)) adder_15 (.a(CNT_14), .b(6'b000001), .out(INC_15));  // open: cin, cout
  Multiplexer #(.width(6)) multiplexer_16 (.in0(INC_15), .in1({6{1'b0}}), .out(CNT_15), .sel(not_1_out[15]));
  Adder #(.width(6)) adder_16 (.a(CNT_15), .b(6'b000001), .out(INC_16));  // open: cin, cout
  Multiplexer #(.width(6)) multiplexer_17 (.in0(INC_16), .in1({6{1'b0}}), .out(CNT_16), .sel(not_1_out[16]));
  Adder #(.width(6)) adder_17 (.a(CNT_16), .b(6'b000001), .out(INC_17));  // open: cin, cout
  Multiplexer #(.width(6)) multiplexer_18 (.in0(INC_17), .in1({6{1'b0}}), .out(CNT_17), .sel(not_1_out[17]));
  Adder #(.width(6)) adder_18 (.a(CNT_17), .b(6'b000001), .out(INC_18));  // open: cin, cout
  Multiplexer #(.width(6)) multiplexer_19 (.in0(INC_18), .in1({6{1'b0}}), .out(CNT_18), .sel(not_1_out[18]));
  Adder #(.width(6)) adder_19 (.a(CNT_18), .b(6'b000001), .out(INC_19));  // open: cin, cout
  Multiplexer #(.width(6)) multiplexer_20 (.in0(INC_19), .in1({6{1'b0}}), .out(CNT_19), .sel(not_1_out[19]));
  Adder #(.width(6)) adder_20 (.a(CNT_19), .b(6'b000001), .out(INC_20));  // open: cin, cout
  Multiplexer #(.width(6)) multiplexer_21 (.in0(INC_20), .in1({6{1'b0}}), .out(CNT_20), .sel(not_1_out[20]));
  Adder #(.width(6)) adder_21 (.a(CNT_20), .b(6'b000001), .out(INC_21));  // open: cin, cout
  Multiplexer #(.width(6)) multiplexer_22 (.in0(INC_21), .in1({6{1'b0}}), .out(CNT_21), .sel(not_1_out[21]));
  Adder #(.width(6)) adder_22 (.a(CNT_21), .b(6'b000001), .out(INC_22));  // open: cin, cout
  Multiplexer #(.width(6)) multiplexer_23 (.in0(INC_22), .in1({6{1'b0}}), .out(CNT_22), .sel(not_1_out[22]));
  Adder #(.width(6)) adder_23 (.a(CNT_22), .b(6'b000001), .out(INC_23));  // open: cin, cout
  Multiplexer #(.width(6)) multiplexer_24 (.in0(INC_23), .in1({6{1'b0}}), .out(CNT_23), .sel(not_1_out[23]));
  Adder #(.width(6)) adder_24 (.a(CNT_23), .b(6'b000001), .out(INC_24));  // open: cin, cout
  Multiplexer #(.width(6)) multiplexer_25 (.in0(INC_24), .in1({6{1'b0}}), .out(CNT_24), .sel(not_1_out[24]));
  Adder #(.width(6)) adder_25 (.a(CNT_24), .b(6'b000001), .out(INC_25));  // open: cin, cout
  Multiplexer #(.width(6)) multiplexer_26 (.in0(INC_25), .in1({6{1'b0}}), .out(CNT_25), .sel(not_1_out[25]));
  Adder #(.width(6)) adder_26 (.a(CNT_25), .b(6'b000001), .out(INC_26));  // open: cin, cout
  Multiplexer #(.width(6)) multiplexer_27 (.in0(INC_26), .in1({6{1'b0}}), .out(CNT_26), .sel(not_1_out[26]));
  Adder #(.width(6)) adder_27 (.a(CNT_26), .b(6'b000001), .out(INC_27));  // open: cin, cout
  Multiplexer #(.width(6)) multiplexer_28 (.in0(INC_27), .in1({6{1'b0}}), .out(CNT_27), .sel(not_1_out[27]));
  Adder #(.width(6)) adder_28 (.a(CNT_27), .b(6'b000001), .out(INC_28));  // open: cin, cout
  Multiplexer #(.width(6)) multiplexer_29 (.in0(INC_28), .in1({6{1'b0}}), .out(CNT_28), .sel(not_1_out[28]));
  Adder #(.width(6)) adder_29 (.a(CNT_28), .b(6'b000001), .out(INC_29));  // open: cin, cout
  Multiplexer #(.width(6)) multiplexer_30 (.in0(INC_29), .in1({6{1'b0}}), .out(CNT_29), .sel(not_1_out[29]));
  Adder #(.width(6)) adder_30 (.a(CNT_29), .b(6'b000001), .out(INC_30));  // open: cin, cout
  Multiplexer #(.width(6)) multiplexer_31 (.in0(INC_30), .in1({6{1'b0}}), .out(CNT_30), .sel(not_1_out[30]));
  Adder #(.width(6)) adder_31 (.a(CNT_30), .b(6'b000001), .out(INC_31));  // open: cin, cout
  Multiplexer #(.width(6)) multiplexer_32 (
    .in0(INC_31), .in1({6{1'b0}}), .out(multiplexer_32_out), .sel(not_1_out[31]));
  assign out1 = {{58{1'b0}}, multiplexer_32_out};  // Bit_Extender bit_extender_1
endmodule

module ROTR_32BIT (
  input  [31:0] b,
  input  [31:0] a,
  output [63:0] out1,
  output done
);

  wire [31:0] multiplexer_1_out, multiplexer_2_out, multiplexer_3_out, multiplexer_4_out, multiplexer_5_out;

  Multiplexer #(.width(32)) multiplexer_1 (.in0(a), .in1({a[15:0], a[31:16]}), .out(multiplexer_1_out), .sel(b[4]));
  Multiplexer #(.width(32)) multiplexer_2 (
    .in0(multiplexer_1_out), .in1({multiplexer_1_out[7:0], multiplexer_1_out[31:8]}),
    .out(multiplexer_2_out), .sel(b[3]));
  Multiplexer #(.width(32)) multiplexer_3 (
    .in0(multiplexer_2_out), .in1({multiplexer_2_out[3:0], multiplexer_2_out[31:4]}),
    .out(multiplexer_3_out), .sel(b[2]));
  Multiplexer #(.width(32)) multiplexer_4 (
    .in0(multiplexer_3_out), .in1({multiplexer_3_out[1:0], multiplexer_3_out[31:2]}),
    .out(multiplexer_4_out), .sel(b[1]));
  Multiplexer #(.width(32)) multiplexer_5 (
    .in0(multiplexer_4_out), .in1({multiplexer_4_out[0], multiplexer_4_out[31:1]}), .out(multiplexer_5_out),
    .sel(b[0]));
  assign out1 = {{32{1'b0}}, multiplexer_5_out};  // Bit_Extender bit_extender_1

  assign done = 1'b1;

  // Other names for the same wires on the sheet: B_0BIT = b[0]; B_1BIT = b[1]; B_2BIT = b[2]; B_3BIT = b[3];
  //   B_4BIT = b[4]
endmodule
